// Logisim project BHT.circ as structural Verilog: 5 circuits, main circuit main
module main (
  input  clk,
  input  jump_suc_3,
  input  hit_3,
  input  rst,
  input  jb_3,
  input  [2:0] hit_pos_3,
  input  [31:0] pc,
  input  [31:0] pc_3,
  input  [31:0] dest_addr,
  output jump_att,
  output hit,
  output [31:0] pc_att,
  output [2:0] hit_pos
);

  wire and_1_out, and_10_out, and_11_out, and_12_out, and_13_out, and_14_out, and_15_out, and_24_out,
       comparator_1_eq, comparator_2_eq, comparator_3_eq, comparator_4_eq, comparator_5_eq, comparator_6_eq,
       comparator_7_eq, comparator_8_eq, empty, en0, en0addr, en1, en1addr, en2, en2addr, en3, en3addr, en4,
       en4addr, en5, en5addr, en6, en6addr, en7, en7addr, nhit_3, not_2_out, not_3_out, not_4_out, not_5_out,
       not_6_out, not_7_out, not_8_out, not_9_out, priority_encoder_2_gs, register_1_q, register_2_q,
       register_3_q, register_4_q, register_5_q, register_6_q, register_7_q, register_8_q, \译码器_1_k0 ,
       \译码器_1_k1 , \译码器_1_k2 , \译码器_1_k3 , \译码器_1_k4 , \译码器_1_k5 , \译码器_1_k6 , \译码器_1_k7 ;
  wire [0:0] multiplexer_5_out;
  wire [1:0] register_25_q, register_26_q, register_27_q, register_28_q, register_29_q, register_30_q,
       register_31_q, register_32_q, \状态机_1_nextstate , \状态机_2_nextstate , \状态机_3_nextstate ,
       \状态机_4_nextstate , \状态机_5_nextstate , \状态机_6_nextstate , \状态机_7_nextstate , \状态机_8_nextstate ;
  wire [2:0] big_num, curr_pos, invalid, multiplexer_1_out, multiplexer_3_out;
  wire [31:0] adder_1_out, adder_2_out, adder_3_out, adder_4_out, adder_5_out, adder_6_out, adder_7_out,
       adder_8_out, multiplexer_6_out, multiplexer_7_out, multiplexer_8_out, multiplexer_9_out,
       multiplexer_10_out, multiplexer_11_out, multiplexer_12_out, multiplexer_13_out, register_9_q,
       register_10_q, register_11_q, register_12_q, register_13_q, register_14_q, register_15_q,
       register_16_q, register_17_q, register_18_q, register_19_q, register_20_q, register_21_q,
       register_22_q, register_23_q, register_24_q, register_33_q, register_34_q, register_35_q,
       register_36_q, register_37_q, register_38_q, register_39_q, register_40_q, \最大数 ;

  Multiplexer #(.width(3), .enable("false")) multiplexer_1 (
    .in0(big_num), .in1(invalid), .out(multiplexer_1_out), .sel(empty));
  Multiplexer #(.width(3), .enable("false")) multiplexer_2 (
    .in0(multiplexer_1_out), .in1(hit_pos_3), .out(curr_pos), .sel(hit_3));
  Register #(.width(1)) register_1 (.D(1'b1), .en(en0), .Q(register_1_q), .clk(clk), .clr(rst));
  Register #(.width(1)) register_2 (.D(1'b1), .en(en1), .Q(register_2_q), .clk(clk), .clr(rst));
  Register #(.width(1)) register_3 (.D(1'b1), .en(en2), .Q(register_3_q), .clk(clk), .clr(rst));
  Register #(.width(1)) register_4 (.D(1'b1), .en(en3), .Q(register_4_q), .clk(clk), .clr(rst));
  Register #(.width(1)) register_5 (.D(1'b1), .en(en4), .Q(register_5_q), .clk(clk), .clr(rst));
  Register #(.width(1)) register_6 (.D(1'b1), .en(en5), .Q(register_6_q), .clk(clk), .clr(rst));
  Register #(.width(1)) register_7 (.D(1'b1), .en(en6), .Q(register_7_q), .clk(clk), .clr(rst));
  Register #(.width(1)) register_8 (.D(1'b1), .en(en7), .Q(register_8_q), .clk(clk), .clr(rst));
  \译码器  \u_译码器_1  (
    .code(curr_pos), .k0(\译码器_1_k0 ), .k1(\译码器_1_k1 ), .k2(\译码器_1_k2 ), .k3(\译码器_1_k3 ), .k4(\译码器_1_k4 ),
    .k5(\译码器_1_k5 ), .k6(\译码器_1_k6 ), .k7(\译码器_1_k7 ));
  not not_1 (nhit_3, hit_3);
  not not_2 (not_2_out, register_1_q);
  not not_3 (not_3_out, register_2_q);
  not not_4 (not_4_out, register_3_q);
  not not_5 (not_5_out, register_4_q);
  Priority_Encoder priority_encoder_1 (
    .in0(not_2_out), .in1(not_3_out), .in2(not_4_out), .in3(not_5_out), .in4(not_6_out), .in5(not_7_out),
    .in6(not_8_out), .in7(not_9_out), .out(invalid), .gs(empty));  // open: en_in, en_out
  not not_6 (not_6_out, register_5_q);
  not not_7 (not_7_out, register_6_q);
  not not_8 (not_8_out, register_7_q);
  not not_9 (not_9_out, register_8_q);
  and and_1 (and_1_out, register_8_q, comparator_8_eq);
  and and_2 (en0, jb_3, \译码器_1_k0 );
  and and_3 (en1, \译码器_1_k1 , jb_3);
  and and_4 (en2, \译码器_1_k2 , jb_3);
  and and_5 (en3, \译码器_1_k3 , jb_3);
  and and_6 (en4, \译码器_1_k4 , jb_3);
  and and_7 (en5, \译码器_1_k5 , jb_3);
  and and_8 (en6, \译码器_1_k6 , jb_3);
  and and_9 (en7, \译码器_1_k7 , jb_3);
  and and_10 (and_10_out, register_5_q, comparator_5_eq);
  and and_11 (and_11_out, register_6_q, comparator_6_eq);
  and and_12 (and_12_out, register_7_q, comparator_7_eq);
  Register #(.width(32)) register_9 (.D(pc_3), .en(en0addr), .Q(register_9_q), .clk(clk), .clr(rst));
  Register #(.width(32)) register_10 (.D(pc_3), .en(en1addr), .Q(register_10_q), .clk(clk), .clr(rst));
  Register #(.width(32)) register_11 (.D(pc_3), .en(en2addr), .Q(register_11_q), .clk(clk), .clr(rst));
  Register #(.width(32)) register_12 (.D(pc_3), .en(en3addr), .Q(register_12_q), .clk(clk), .clr(rst));
  Register #(.width(32)) register_13 (.D(pc_3), .en(en4addr), .Q(register_13_q), .clk(clk), .clr(rst));
  Register #(.width(32)) register_14 (.D(pc_3), .en(en5addr), .Q(register_14_q), .clk(clk), .clr(rst));
  Register #(.width(32)) register_15 (.D(pc_3), .en(en6addr), .Q(register_15_q), .clk(clk), .clr(rst));
  Register #(.width(32)) register_16 (.D(pc_3), .en(en7addr), .Q(register_16_q), .clk(clk), .clr(rst));
  and and_13 (and_13_out, register_4_q, comparator_4_eq);
  and and_14 (and_14_out, register_2_q, comparator_2_eq);
  and and_15 (and_15_out, register_3_q, comparator_3_eq);
  or or_1 (hit, and_1_out, and_12_out, and_11_out, and_10_out, and_13_out, and_15_out, and_14_out, and_24_out);
  and and_16 (en0addr, nhit_3, en0);
  and and_17 (en1addr, nhit_3, en1);
  and and_18 (en2addr, nhit_3, en2);
  and and_19 (en3addr, nhit_3, en3);
  and and_20 (en4addr, nhit_3, en4);
  and and_21 (en5addr, nhit_3, en5);
  and and_22 (en6addr, nhit_3, en6);
  and and_23 (en7addr, nhit_3, en7);
  Comparator #(.width(32)) comparator_1 (.a(pc), .b(register_9_q), .eq(comparator_1_eq));  // open: gt, lt
  Comparator #(.width(32)) comparator_2 (.a(pc), .b(register_10_q), .eq(comparator_2_eq));  // open: gt, lt
  Comparator #(.width(32)) comparator_3 (.a(pc), .b(register_11_q), .eq(comparator_3_eq));  // open: gt, lt
  Comparator #(.width(32)) comparator_4 (.a(pc), .b(register_12_q), .eq(comparator_4_eq));  // open: gt, lt
  Comparator #(.width(32)) comparator_5 (.a(pc), .b(register_13_q), .eq(comparator_5_eq));  // open: gt, lt
  Comparator #(.width(32)) comparator_6 (.a(pc), .b(register_14_q), .eq(comparator_6_eq));  // open: gt, lt
  Comparator #(.width(32)) comparator_7 (.a(pc), .b(register_15_q), .eq(comparator_7_eq));  // open: gt, lt
  Comparator #(.width(32)) comparator_8 (.a(pc), .b(register_16_q), .eq(comparator_8_eq));  // open: gt, lt
  and and_24 (and_24_out, register_1_q, comparator_1_eq);
  Priority_Encoder priority_encoder_2 (
    .in0(and_24_out), .in1(and_14_out), .in2(and_15_out), .in3(and_13_out), .in4(and_10_out),
    .in5(and_11_out), .in6(and_12_out), .in7(and_1_out), .out(hit_pos), .gs(priority_encoder_2_gs));  // open: en_in, en_out
  Multiplexer #(.width(3), .enable("false")) multiplexer_3 (
    .in0(3'b000), .in1(hit_pos), .out(multiplexer_3_out), .sel(priority_encoder_2_gs));
  Register #(.width(32)) register_17 (.D(dest_addr), .en(en0addr), .Q(register_17_q), .clk(clk), .clr(rst));
  Register #(.width(32)) register_18 (.D(dest_addr), .en(en1addr), .Q(register_18_q), .clk(clk), .clr(rst));
  Register #(.width(32)) register_19 (.D(dest_addr), .en(en2addr), .Q(register_19_q), .clk(clk), .clr(rst));
  Register #(.width(32)) register_20 (.D(dest_addr), .en(en3addr), .Q(register_20_q), .clk(clk), .clr(rst));
  Register #(.width(32)) register_21 (.D(dest_addr), .en(en4addr), .Q(register_21_q), .clk(clk), .clr(rst));
  Register #(.width(32)) register_22 (.D(dest_addr), .en(en5addr), .Q(register_22_q), .clk(clk), .clr(rst));
  Register #(.width(32)) register_23 (.D(dest_addr), .en(en6addr), .Q(register_23_q), .clk(clk), .clr(rst));
  Register #(.width(32)) register_24 (.D(dest_addr), .en(en7addr), .Q(register_24_q), .clk(clk), .clr(rst));
  Multiplexer #(.select(3), .width(32), .enable("false")) multiplexer_4 (
    .in0(register_17_q), .in1(register_18_q), .in2(register_19_q), .in3(register_20_q), .in4(register_21_q),
    .in5(register_22_q), .in6(register_23_q), .in7(register_24_q), .out(pc_att), .sel(multiplexer_3_out));
  \状态机  \u_状态机_1  (.state(register_25_q), .nextstate(\状态机_1_nextstate ), .hit_jump({hit_3, jump_suc_3}));
  \状态机  \u_状态机_2  (.state(register_26_q), .nextstate(\状态机_2_nextstate ), .hit_jump({hit_3, jump_suc_3}));
  \状态机  \u_状态机_3  (.state(register_27_q), .nextstate(\状态机_3_nextstate ), .hit_jump({hit_3, jump_suc_3}));
  \状态机  \u_状态机_4  (.state(register_28_q), .nextstate(\状态机_4_nextstate ), .hit_jump({hit_3, jump_suc_3}));
  \状态机  \u_状态机_5  (.state(register_29_q), .nextstate(\状态机_5_nextstate ), .hit_jump({hit_3, jump_suc_3}));
  \状态机  \u_状态机_6  (.state(register_30_q), .nextstate(\状态机_6_nextstate ), .hit_jump({hit_3, jump_suc_3}));
  \状态机  \u_状态机_7  (.state(register_31_q), .nextstate(\状态机_7_nextstate ), .hit_jump({hit_3, jump_suc_3}));
  \状态机  \u_状态机_8  (.state(register_32_q), .nextstate(\状态机_8_nextstate ), .hit_jump({hit_3, jump_suc_3}));
  Register #(.width(2)) register_25 (.D(\状态机_1_nextstate ), .en(en0), .Q(register_25_q), .clk(clk), .clr(rst));
  Register #(.width(2)) register_26 (.D(\状态机_2_nextstate ), .en(en1), .Q(register_26_q), .clk(clk), .clr(rst));
  Register #(.width(2)) register_27 (.D(\状态机_3_nextstate ), .en(en2), .Q(register_27_q), .clk(clk), .clr(rst));
  Register #(.width(2)) register_28 (.D(\状态机_4_nextstate ), .en(en3), .Q(register_28_q), .clk(clk), .clr(rst));
  Register #(.width(2)) register_29 (.D(\状态机_5_nextstate ), .en(en4), .Q(register_29_q), .clk(clk), .clr(rst));
  Register #(.width(2)) register_30 (.D(\状态机_6_nextstate ), .en(en5), .Q(register_30_q), .clk(clk), .clr(rst));
  Register #(.width(2)) register_31 (.D(\状态机_7_nextstate ), .en(en6), .Q(register_31_q), .clk(clk), .clr(rst));
  Register #(.width(2)) register_32 (.D(\状态机_8_nextstate ), .en(en7), .Q(register_32_q), .clk(clk), .clr(rst));
  Multiplexer #(.select(3), .width(2), .enable("false")) multiplexer_5 (
    .in0(register_25_q), .in1(register_26_q), .in2(register_27_q), .in3(register_28_q), .in4(register_29_q),
    .in5(register_30_q), .in6(register_31_q), .in7(register_32_q), .out({jump_att, multiplexer_5_out[0]}),
    .sel(multiplexer_3_out));
  Multiplexer #(.width(32), .enable("false")) multiplexer_6 (
    .in0(adder_1_out), .in1({32{1'b0}}), .out(multiplexer_6_out), .sel(en0));
  Multiplexer #(.width(32), .enable("false")) multiplexer_7 (
    .in0(adder_2_out), .in1({32{1'b0}}), .out(multiplexer_7_out), .sel(en1));
  Multiplexer #(.width(32), .enable("false")) multiplexer_8 (
    .in0(adder_3_out), .in1({32{1'b0}}), .out(multiplexer_8_out), .sel(en2));
  Multiplexer #(.width(32), .enable("false")) multiplexer_9 (
    .in0(adder_4_out), .in1({32{1'b0}}), .out(multiplexer_9_out), .sel(en3));
  Multiplexer #(.width(32), .enable("false")) multiplexer_10 (
    .in0(adder_5_out), .in1({32{1'b0}}), .out(multiplexer_10_out), .sel(en4));
  Multiplexer #(.width(32), .enable("false")) multiplexer_11 (
    .in0(adder_6_out), .in1({32{1'b0}}), .out(multiplexer_11_out), .sel(en5));
  Multiplexer #(.width(32), .enable("false")) multiplexer_12 (
    .in0(adder_7_out), .in1({32{1'b0}}), .out(multiplexer_12_out), .sel(en6));
  Multiplexer #(.width(32), .enable("false")) multiplexer_13 (
    .in0(adder_8_out), .in1({32{1'b0}}), .out(multiplexer_13_out), .sel(en7));
  Register #(.width(32)) register_33 (.D(multiplexer_6_out), .en(jb_3), .Q(register_33_q), .clk(clk), .clr(rst));
  Register #(.width(32)) register_34 (.D(multiplexer_7_out), .en(jb_3), .Q(register_34_q), .clk(clk), .clr(rst));
  Register #(.width(32)) register_35 (.D(multiplexer_8_out), .en(jb_3), .Q(register_35_q), .clk(clk), .clr(rst));
  Register #(.width(32)) register_36 (.D(multiplexer_9_out), .en(jb_3), .Q(register_36_q), .clk(clk), .clr(rst));
  Register #(.width(32)) register_37 (.D(multiplexer_10_out), .en(jb_3), .Q(register_37_q), .clk(clk), .clr(rst));
  Register #(.width(32)) register_38 (.D(multiplexer_11_out), .en(jb_3), .Q(register_38_q), .clk(clk), .clr(rst));
  Register #(.width(32)) register_39 (.D(multiplexer_12_out), .en(jb_3), .Q(register_39_q), .clk(clk), .clr(rst));
  Register #(.width(32)) register_40 (.D(multiplexer_13_out), .en(jb_3), .Q(register_40_q), .clk(clk), .clr(rst));
  Adder #(.width(32)) adder_1 (.a(32'h1), .b(register_33_q), .out(adder_1_out));  // open: cin, cout
  Adder #(.width(32)) adder_2 (.a(32'h1), .b(register_34_q), .out(adder_2_out));  // open: cin, cout
  Adder #(.width(32)) adder_3 (.a(32'h1), .b(register_35_q), .out(adder_3_out));  // open: cin, cout
  Adder #(.width(32)) adder_4 (.a(32'h1), .b(register_36_q), .out(adder_4_out));  // open: cin, cout
  Adder #(.width(32)) adder_5 (.a(32'h1), .b(register_37_q), .out(adder_5_out));  // open: cin, cout
  Adder #(.width(32)) adder_6 (.a(32'h1), .b(register_38_q), .out(adder_6_out));  // open: cin, cout
  Adder #(.width(32)) adder_7 (.a(32'h1), .b(register_39_q), .out(adder_7_out));  // open: cin, cout
  Adder #(.width(32)) adder_8 (.a(32'h1), .b(register_40_q), .out(adder_8_out));  // open: cin, cout
  \最大数  \u_最大数_1  (
    ._000(register_33_q), ._001(register_34_q), ._010(register_35_q), ._011(register_36_q),
    ._100(register_37_q), ._101(register_38_q), ._110(register_39_q), ._111(register_40_q), .\最大数 (\最大数 ),
    .\最大编号 (big_num));

  // Notes on the sheet:
  //   valid
  //   指令addr
  //   目标addr
  //   预测历史
  //   LRU
endmodule

module \状态  (
  input  [1:0] status,
  input  jump,
  output [1:0] next_status
);

  wire and_1_out, and_2_out, and_3_out;

  and and_1 (and_1_out, status[0], jump);
  and and_2 (and_2_out, status[1], jump);
  and and_3 (and_3_out, status[1], status[0]);
  or or_1 (next_status[1], and_1_out, and_2_out, and_3_out);

  assign next_status[0] = jump;
endmodule

module \状态机  (
  input  [1:0] state,
  input  [1:0] hit_jump,
  output [1:0] nextstate
);

  wire [1:0] \状态_1_next_status , \状态_2_next_status ;

  \状态  \u_状态_1  (.status(state), .jump(1'b0), .next_status(\状态_1_next_status ));
  \状态  \u_状态_2  (.status(state), .jump(1'b1), .next_status(\状态_2_next_status ));
  Multiplexer #(.select(2), .width(2), .enable("false")) multiplexer_1 (
    .in0(2'b01), .in1(2'b10), .in2(\状态_1_next_status ), .in3(\状态_2_next_status ), .out(nextstate),
    .sel(hit_jump));
endmodule

module \最大数  (
  input  [31:0] _000,
  input  [31:0] _001,
  input  [31:0] _010,
  input  [31:0] _011,
  input  [31:0] _100,
  input  [31:0] _101,
  input  [31:0] _110,
  input  [31:0] _111,
  output [31:0] \最大数 ,
  output [2:0] \最大编号 
);

  wire comparator_1_lt, comparator_2_lt, comparator_3_lt, comparator_4_lt, comparator_5_lt, comparator_6_lt,
       comparator_7_lt;
  wire [2:0] multiplexer_2_out, multiplexer_4_out, multiplexer_6_out, multiplexer_8_out, multiplexer_10_out,
       multiplexer_12_out;
  wire [31:0] multiplexer_1_out, multiplexer_3_out, multiplexer_5_out, multiplexer_7_out, multiplexer_9_out,
       multiplexer_11_out;

  Comparator #(.width(32)) comparator_1 (.a(_000), .b(_001), .lt(comparator_1_lt));  // open: gt, eq
  Comparator #(.width(32)) comparator_2 (.a(_010), .b(_011), .lt(comparator_2_lt));  // open: gt, eq
  Comparator #(.width(32)) comparator_3 (.a(_100), .b(_101), .lt(comparator_3_lt));  // open: gt, eq
  Comparator #(.width(32)) comparator_4 (.a(_110), .b(_111), .lt(comparator_4_lt));  // open: gt, eq
  Multiplexer #(.width(32), .enable("false")) multiplexer_1 (
    .in0(_000), .in1(_001), .out(multiplexer_1_out), .sel(comparator_1_lt));
  Multiplexer #(.width(3), .enable("false")) multiplexer_2 (
    .in0(3'b000), .in1(3'b001), .out(multiplexer_2_out), .sel(comparator_1_lt));
  Multiplexer #(.width(32), .enable("false")) multiplexer_3 (
    .in0(_010), .in1(_011), .out(multiplexer_3_out), .sel(comparator_2_lt));
  Multiplexer #(.width(3), .enable("false")) multiplexer_4 (
    .in0(3'b010), .in1(3'b011), .out(multiplexer_4_out), .sel(comparator_2_lt));
  Multiplexer #(.width(32), .enable("false")) multiplexer_5 (
    .in0(_100), .in1(_101), .out(multiplexer_5_out), .sel(comparator_3_lt));
  Multiplexer #(.width(3), .enable("false")) multiplexer_6 (
    .in0(3'b100), .in1(3'b101), .out(multiplexer_6_out), .sel(comparator_3_lt));
  Multiplexer #(.width(32), .enable("false")) multiplexer_7 (
    .in0(_110), .in1(_111), .out(multiplexer_7_out), .sel(comparator_4_lt));
  Multiplexer #(.width(3), .enable("false")) multiplexer_8 (
    .in0(3'b110), .in1(3'b111), .out(multiplexer_8_out), .sel(comparator_4_lt));
  Comparator #(.width(32)) comparator_5 (
    .a(multiplexer_1_out), .b(multiplexer_3_out), .lt(comparator_5_lt));  // open: gt, eq
  Comparator #(.width(32)) comparator_6 (
    .a(multiplexer_5_out), .b(multiplexer_7_out), .lt(comparator_6_lt));  // open: gt, eq
  Multiplexer #(.width(32), .enable("false")) multiplexer_9 (
    .in0(multiplexer_1_out), .in1(multiplexer_3_out), .out(multiplexer_9_out), .sel(comparator_5_lt));
  Multiplexer #(.width(3), .enable("false")) multiplexer_10 (
    .in0(multiplexer_2_out), .in1(multiplexer_4_out), .out(multiplexer_10_out), .sel(comparator_5_lt));
  Multiplexer #(.width(32), .enable("false")) multiplexer_11 (
    .in0(multiplexer_5_out), .in1(multiplexer_7_out), .out(multiplexer_11_out), .sel(comparator_6_lt));
  Multiplexer #(.width(3), .enable("false")) multiplexer_12 (
    .in0(multiplexer_6_out), .in1(multiplexer_8_out), .out(multiplexer_12_out), .sel(comparator_6_lt));
  Comparator #(.width(32)) comparator_7 (
    .a(multiplexer_9_out), .b(multiplexer_11_out), .lt(comparator_7_lt));  // open: gt, eq
  Multiplexer #(.width(32), .enable("false")) multiplexer_13 (
    .in0(multiplexer_9_out), .in1(multiplexer_11_out), .out(\最大数 ), .sel(comparator_7_lt));
  Multiplexer #(.width(3), .enable("false")) multiplexer_14 (
    .in0(multiplexer_10_out), .in1(multiplexer_12_out), .out(\最大编号 ), .sel(comparator_7_lt));
endmodule

module \译码器  (
  input  [2:0] code,
  output k0,
  output k1,
  output k2,
  output k3,
  output k4,
  output k5,
  output k6,
  output k7
);

  wire not_1_out, not_2_out, not_3_out, not_4_out, not_5_out, not_6_out, not_7_out, not_8_out, not_9_out,
       not_10_out, not_11_out, not_12_out;

  not not_1 (not_1_out, code[2]);
  not not_2 (not_2_out, code[1]);
  not not_3 (not_3_out, code[0]);
  not not_4 (not_4_out, code[2]);
  not not_5 (not_5_out, code[1]);
  not not_6 (not_6_out, code[2]);
  not not_7 (not_7_out, code[0]);
  not not_8 (not_8_out, code[2]);
  not not_9 (not_9_out, code[1]);
  not not_10 (not_10_out, code[0]);
  not not_11 (not_11_out, code[1]);
  not not_12 (not_12_out, code[0]);
  and and_1 (k7, code[2], code[1], code[0]);
  and and_2 (k0, not_1_out, not_2_out, not_3_out);
  and and_3 (k1, not_4_out, not_5_out, code[0]);
  and and_4 (k2, not_6_out, code[1], not_7_out);
  and and_5 (k3, not_8_out, code[1], code[0]);
  and and_6 (k4, code[2], not_9_out, not_10_out);
  and and_7 (k5, code[2], not_11_out, code[0]);
  and and_8 (k6, code[2], code[1], not_12_out);
endmodule
