// Logisim project BHT林力韬.circ as structural Verilog: 5 circuits, main circuit main
module main (
  input  [31:0] PC,
  input  [31:0] EX_PC,
  input  [31:0] PC_4,
  input  [31:0] Addr,
  input  HIT,
  input  JUMP,
  input  J_INS,
  input  [2:0] HIT_POS,
  input  clk,
  input  rst,
  output [31:0] PC_OUT,
  output \跳转 ,
  output [2:0] \命中位置 ,
  output \命中 
);

  wire ACTEN0, ACTEN1, ACTEN2, ACTEN3, ACTEN4, ACTEN5, ACTEN6, ACTEN7, and_9_out, and_10_out, and_11_out,
       and_12_out, and_13_out, and_14_out, and_15_out, and_16_out, and_17_out, and_18_out, and_19_out,
       and_20_out, and_21_out, and_22_out, and_23_out, and_24_out, and_25_out, and_26_out, and_27_out,
       and_28_out, and_29_out, and_30_out, and_31_out, and_32_out, comparator_1_eq, comparator_2_eq,
       comparator_3_eq, comparator_4_eq, comparator_5_eq, comparator_6_eq, comparator_7_eq, comparator_8_eq,
       EN0, EN1, EN2, EN3, EN4, EN5, EN6, EN7, Have_Invalid, NO_HIT, not_2_out, not_3_out, not_4_out,
       not_5_out, not_6_out, not_7_out, not_8_out, not_9_out, priority_encoder_2_gs, valid_2_q, valid_3_q,
       valid_4_q, valid_5_q, valid_6_q, valid_7_q, valid_8_q, valid_q;
  wire [0:0] multiplexer_7_out;
  wire [1:0] new_status_1_new_status, new_status_2_new_status, new_status_3_new_status,
       new_status_4_new_status, new_status_5_new_status, new_status_6_new_status, new_status_7_new_status,
       new_status_8_new_status, status_2_q, status_3_q, status_4_q, status_5_q, status_6_q, status_7_q,
       status_8_q, status_q;
  wire [2:0] ACT_POS, BiggestCode, Invalid_Pos, multiplexer_1_out, priority_encoder_2_out;
  wire [31:0] adder_1_out, adder_2_out, adder_3_out, adder_4_out, adder_5_out, adder_6_out, adder_7_out,
       adder_8_out, Addr_2_q, Addr_3_q, Addr_4_q, Addr_5_q, Addr_6_q, Addr_7_q, Addr_8_q, Addr_q,
       LRU_num_2_q, LRU_num_3_q, LRU_num_4_q, LRU_num_5_q, LRU_num_6_q, LRU_num_7_q, LRU_num_8_q, LRU_num_q,
       multiplexer_5_out, multiplexer_6_out, multiplexer_8_out, multiplexer_9_out, multiplexer_10_out,
       multiplexer_11_out, multiplexer_12_out, multiplexer_13_out, multiplexer_14_out, multiplexer_15_out,
       PC_2_q, PC_3_q, PC_4_q, PC_5_q, PC_6_q, PC_7_q, PC_8_q, PC_q;

  // Probe on Invalid_Pos
  Multiplexer #(.width(3)) multiplexer_1 (
    .in0(BiggestCode), .in1(Invalid_Pos), .out(multiplexer_1_out), .sel(Have_Invalid));  // open: en
  // Probe on BiggestCode
  decoder decoder_1 (.code(ACT_POS), .k0(EN0), .k1(EN1), .k2(EN2), .k3(EN3), .k4(EN4), .k5(EN5), .k6(EN6), .k7(EN7));
  and and_1 (ACTEN0, J_INS, EN0);
  and and_2 (ACTEN1, J_INS, EN1);
  and and_3 (ACTEN4, J_INS, EN4);
  and and_4 (ACTEN5, J_INS, EN5);
  and and_5 (ACTEN6, J_INS, EN6);
  and and_6 (ACTEN7, J_INS, EN7);
  or or_1 (\命中 , and_15_out, and_16_out, and_14_out, and_13_out, and_12_out, and_11_out, and_10_out, and_9_out);
  not not_1 (NO_HIT, HIT);
  Multiplexer #(.width(3)) multiplexer_2 (
    .in0(multiplexer_1_out), .in1(HIT_POS), .out(ACT_POS), .sel(HIT));  // open: en
  and and_7 (ACTEN2, J_INS, EN2);
  and and_8 (ACTEN3, J_INS, EN3);
  and and_9 (and_9_out, valid_8_q, comparator_8_eq);
  // Probe on ACT_POS
  and and_10 (and_10_out, valid_7_q, comparator_7_eq);
  and and_11 (and_11_out, valid_6_q, comparator_6_eq);
  D_Flip_Flop valid (.clk(clk), .D(1'b1), .Q(valid_q), .en(ACTEN0), .reset(rst));  // open: Qn, preset
  D_Flip_Flop valid_2 (.clk(clk), .D(1'b1), .Q(valid_2_q), .en(ACTEN1), .reset(rst));  // open: Qn, preset
  D_Flip_Flop valid_3 (.clk(clk), .D(1'b1), .Q(valid_3_q), .en(ACTEN2), .reset(rst));  // open: Qn, preset
  D_Flip_Flop valid_4 (.clk(clk), .D(1'b1), .Q(valid_4_q), .en(ACTEN3), .reset(rst));  // open: Qn, preset
  D_Flip_Flop valid_5 (.clk(clk), .D(1'b1), .Q(valid_5_q), .en(ACTEN4), .reset(rst));  // open: Qn, preset
  D_Flip_Flop valid_6 (.clk(clk), .D(1'b1), .Q(valid_6_q), .en(ACTEN5), .reset(rst));  // open: Qn, preset
  D_Flip_Flop valid_7 (.clk(clk), .D(1'b1), .Q(valid_7_q), .en(ACTEN6), .reset(rst));  // open: Qn, preset
  D_Flip_Flop valid_8 (.clk(clk), .D(1'b1), .Q(valid_8_q), .en(ACTEN7), .reset(rst));  // open: Qn, preset
  and and_12 (and_12_out, valid_5_q, comparator_5_eq);
  and and_13 (and_13_out, valid_4_q, comparator_2_eq);
  and and_14 (and_14_out, valid_3_q, comparator_1_eq);
  and and_15 (and_15_out, valid_q, comparator_3_eq);
  and and_16 (and_16_out, valid_2_q, comparator_4_eq);
  not not_2 (not_2_out, valid_q);
  not not_3 (not_3_out, valid_2_q);
  not not_4 (not_4_out, valid_3_q);
  Priority_Encoder priority_encoder_1 (
    .in0(not_2_out), .in1(not_3_out), .in2(not_4_out), .in3(not_5_out), .in4(not_6_out), .in5(not_7_out),
    .in6(not_8_out), .in7(not_9_out), .out(Invalid_Pos), .gs(Have_Invalid));  // open: en_in, en_out
  not not_5 (not_5_out, valid_4_q);
  not not_6 (not_6_out, valid_5_q);
  not not_7 (not_7_out, valid_6_q);
  not not_8 (not_8_out, valid_7_q);
  not not_9 (not_9_out, valid_8_q);
  and and_17 (and_17_out, NO_HIT, ACTEN0);
  and and_18 (and_18_out, NO_HIT, ACTEN1);
  and and_19 (and_19_out, NO_HIT, ACTEN2);
  and and_20 (and_20_out, NO_HIT, ACTEN3);
  and and_21 (and_21_out, NO_HIT, ACTEN4);
  and and_22 (and_22_out, NO_HIT, ACTEN5);
  and and_23 (and_23_out, NO_HIT, ACTEN6);
  and and_24 (and_24_out, NO_HIT, ACTEN7);
  Priority_Encoder priority_encoder_2 (
    .in0(and_15_out), .in1(and_16_out), .in2(and_14_out), .in3(and_13_out), .in4(and_12_out),
    .in5(and_11_out), .in6(and_10_out), .in7(and_9_out), .out(priority_encoder_2_out),
    .gs(priority_encoder_2_gs));  // open: en_in, en_out
  // Probe on Invalid_Pos
  Register #(.width(32)) u_PC (.D(EX_PC), .en(and_17_out), .Q(PC_q), .clk(clk), .clr(rst));
  Register #(.width(32)) PC_2 (.D(EX_PC), .en(and_18_out), .Q(PC_2_q), .clk(clk), .clr(rst));
  Register #(.width(32)) PC_3 (.D(EX_PC), .en(and_19_out), .Q(PC_3_q), .clk(clk), .clr(rst));
  Comparator #(.width(32)) comparator_1 (.a(PC_3_q), .b(PC), .eq(comparator_1_eq));  // open: gt, lt
  Register #(.width(32)) u_PC_4 (.D(EX_PC), .en(and_20_out), .Q(PC_4_q), .clk(clk), .clr(rst));
  Comparator #(.width(32)) comparator_2 (.a(PC_4_q), .b(PC), .eq(comparator_2_eq));  // open: gt, lt
  Register #(.width(32)) PC_5 (.D(EX_PC), .en(and_21_out), .Q(PC_5_q), .clk(clk), .clr(rst));
  Register #(.width(32)) PC_6 (.D(EX_PC), .en(and_22_out), .Q(PC_6_q), .clk(clk), .clr(rst));
  Register #(.width(32)) PC_7 (.D(EX_PC), .en(and_23_out), .Q(PC_7_q), .clk(clk), .clr(rst));
  Register #(.width(32)) PC_8 (.D(EX_PC), .en(and_24_out), .Q(PC_8_q), .clk(clk), .clr(rst));
  // Probe on priority_encoder_2_out
  Multiplexer #(.width(32)) multiplexer_3 (.in0(PC_4), .in1(multiplexer_5_out), .out(PC_OUT), .sel(\命中 ));  // open: en
  Comparator #(.width(32)) comparator_3 (.a(PC_q), .b(PC), .eq(comparator_3_eq));  // open: gt, lt
  Comparator #(.width(32)) comparator_4 (.a(PC_2_q), .b(PC), .eq(comparator_4_eq));  // open: gt, lt
  Comparator #(.width(32)) comparator_5 (.a(PC_5_q), .b(PC), .eq(comparator_5_eq));  // open: gt, lt
  Comparator #(.width(32)) comparator_6 (.a(PC_6_q), .b(PC), .eq(comparator_6_eq));  // open: gt, lt
  Comparator #(.width(32)) comparator_7 (.a(PC_7_q), .b(PC), .eq(comparator_7_eq));  // open: gt, lt
  Comparator #(.width(32)) comparator_8 (.a(PC_8_q), .b(PC), .eq(comparator_8_eq));  // open: gt, lt
  Multiplexer #(.width(3)) multiplexer_4 (
    .in0(3'b000), .in1(priority_encoder_2_out), .out(\命中位置 ), .sel(priority_encoder_2_gs));  // open: en
  // Probe on multiplexer_5_out
  and and_25 (and_25_out, NO_HIT, ACTEN0);
  and and_26 (and_26_out, NO_HIT, ACTEN1);
  and and_27 (and_27_out, NO_HIT, ACTEN2);
  and and_28 (and_28_out, NO_HIT, ACTEN3);
  and and_29 (and_29_out, NO_HIT, ACTEN4);
  and and_30 (and_30_out, NO_HIT, ACTEN5);
  and and_31 (and_31_out, NO_HIT, ACTEN6);
  and and_32 (and_32_out, NO_HIT, ACTEN7);
  Multiplexer #(.width(32)) multiplexer_5 (
    .in0(PC_4), .in1(multiplexer_6_out), .out(multiplexer_5_out), .sel(\跳转 ));  // open: en
  Register #(.width(32)) u_Addr (.D(Addr), .en(and_25_out), .Q(Addr_q), .clk(clk), .clr(rst));
  Register #(.width(32)) Addr_2 (.D(Addr), .en(and_26_out), .Q(Addr_2_q), .clk(clk), .clr(rst));
  Register #(.width(32)) Addr_3 (.D(Addr), .en(and_27_out), .Q(Addr_3_q), .clk(clk), .clr(rst));
  Register #(.width(32)) Addr_4 (.D(Addr), .en(and_28_out), .Q(Addr_4_q), .clk(clk), .clr(rst));
  Register #(.width(32)) Addr_5 (.D(Addr), .en(and_29_out), .Q(Addr_5_q), .clk(clk), .clr(rst));
  Register #(.width(32)) Addr_6 (.D(Addr), .en(and_30_out), .Q(Addr_6_q), .clk(clk), .clr(rst));
  Register #(.width(32)) Addr_7 (.D(Addr), .en(and_31_out), .Q(Addr_7_q), .clk(clk), .clr(rst));
  Register #(.width(32)) Addr_8 (.D(Addr), .en(and_32_out), .Q(Addr_8_q), .clk(clk), .clr(rst));
  Multiplexer #(.select(3), .width(32)) multiplexer_6 (
    .in0(Addr_q), .in1(Addr_2_q), .in2(Addr_3_q), .in3(Addr_4_q), .in4(Addr_5_q), .in5(Addr_6_q),
    .in6(Addr_7_q), .in7(Addr_8_q), .out(multiplexer_6_out), .sel(\命中位置 ));  // open: en
  // Probe on multiplexer_6_out
  // Probe on \命中位置 
  new_status new_status_1 (.old_status(status_q), .hit_jump({HIT, JUMP}), .new_status(new_status_1_new_status));
  new_status new_status_2 (.old_status(status_2_q), .hit_jump({HIT, JUMP}), .new_status(new_status_2_new_status));
  new_status new_status_3 (.old_status(status_3_q), .hit_jump({HIT, JUMP}), .new_status(new_status_3_new_status));
  new_status new_status_4 (.old_status(status_4_q), .hit_jump({HIT, JUMP}), .new_status(new_status_4_new_status));
  new_status new_status_5 (.old_status(status_5_q), .hit_jump({HIT, JUMP}), .new_status(new_status_5_new_status));
  new_status new_status_6 (.old_status(status_6_q), .hit_jump({HIT, JUMP}), .new_status(new_status_6_new_status));
  new_status new_status_7 (.old_status(status_7_q), .hit_jump({HIT, JUMP}), .new_status(new_status_7_new_status));
  new_status new_status_8 (.old_status(status_8_q), .hit_jump({HIT, JUMP}), .new_status(new_status_8_new_status));
  Register #(.width(2)) status (.D(new_status_1_new_status), .en(ACTEN0), .Q(status_q), .clk(clk), .clr(rst));
  Register #(.width(2)) status_2 (.D(new_status_2_new_status), .en(ACTEN1), .Q(status_2_q), .clk(clk), .clr(rst));
  Register #(.width(2)) status_3 (.D(new_status_3_new_status), .en(ACTEN2), .Q(status_3_q), .clk(clk), .clr(rst));
  Register #(.width(2)) status_4 (.D(new_status_4_new_status), .en(ACTEN3), .Q(status_4_q), .clk(clk), .clr(rst));
  Register #(.width(2)) status_5 (.D(new_status_5_new_status), .en(ACTEN4), .Q(status_5_q), .clk(clk), .clr(rst));
  Register #(.width(2)) status_6 (.D(new_status_6_new_status), .en(ACTEN5), .Q(status_6_q), .clk(clk), .clr(rst));
  Register #(.width(2)) status_7 (.D(new_status_7_new_status), .en(ACTEN6), .Q(status_7_q), .clk(clk), .clr(rst));
  Register #(.width(2)) status_8 (.D(new_status_8_new_status), .en(ACTEN7), .Q(status_8_q), .clk(clk), .clr(rst));
  Multiplexer #(.select(3), .width(2)) multiplexer_7 (
    .in0(status_q), .in1(status_2_q), .in2(status_3_q), .in3(status_4_q), .in4(status_5_q), .in5(status_6_q),
    .in6(status_7_q), .in7(status_8_q), .out({\跳转 , multiplexer_7_out[0]}), .sel(\命中位置 ));  // open: en
  // Probe on \命中位置 
  // Probe on \命中位置 
  Register #(.width(32)) LRU_num (.D(multiplexer_8_out), .en(J_INS), .Q(LRU_num_q), .clk(clk), .clr(rst));
  Multiplexer #(.width(32)) multiplexer_8 (
    .in0(adder_1_out), .in1({32{1'b0}}), .out(multiplexer_8_out), .sel(ACTEN0));  // open: en
  Multiplexer #(.width(32)) multiplexer_9 (
    .in0(adder_2_out), .in1({32{1'b0}}), .out(multiplexer_9_out), .sel(ACTEN1));  // open: en
  Register #(.width(32)) LRU_num_2 (.D(multiplexer_9_out), .en(J_INS), .Q(LRU_num_2_q), .clk(clk), .clr(rst));
  Register #(.width(32)) LRU_num_3 (.D(multiplexer_10_out), .en(J_INS), .Q(LRU_num_3_q), .clk(clk), .clr(rst));
  Multiplexer #(.width(32)) multiplexer_10 (
    .in0(adder_3_out), .in1({32{1'b0}}), .out(multiplexer_10_out), .sel(ACTEN2));  // open: en
  Register #(.width(32)) LRU_num_4 (.D(multiplexer_11_out), .en(J_INS), .Q(LRU_num_4_q), .clk(clk), .clr(rst));
  Multiplexer #(.width(32)) multiplexer_11 (
    .in0(adder_4_out), .in1({32{1'b0}}), .out(multiplexer_11_out), .sel(ACTEN3));  // open: en
  Register #(.width(32)) LRU_num_5 (.D(multiplexer_12_out), .en(J_INS), .Q(LRU_num_5_q), .clk(clk), .clr(rst));
  Multiplexer #(.width(32)) multiplexer_12 (
    .in0(adder_5_out), .in1({32{1'b0}}), .out(multiplexer_12_out), .sel(ACTEN4));  // open: en
  Multiplexer #(.width(32)) multiplexer_13 (
    .in0(adder_6_out), .in1({32{1'b0}}), .out(multiplexer_13_out), .sel(ACTEN5));  // open: en
  Register #(.width(32)) LRU_num_6 (.D(multiplexer_13_out), .en(J_INS), .Q(LRU_num_6_q), .clk(clk), .clr(rst));
  Multiplexer #(.width(32)) multiplexer_14 (
    .in0(adder_7_out), .in1({32{1'b0}}), .out(multiplexer_14_out), .sel(ACTEN6));  // open: en
  Register #(.width(32)) LRU_num_7 (.D(multiplexer_14_out), .en(J_INS), .Q(LRU_num_7_q), .clk(clk), .clr(rst));
  Multiplexer #(.width(32)) multiplexer_15 (
    .in0(adder_8_out), .in1({32{1'b0}}), .out(multiplexer_15_out), .sel(ACTEN7));  // open: en
  Register #(.width(32)) LRU_num_8 (.D(multiplexer_15_out), .en(J_INS), .Q(LRU_num_8_q), .clk(clk), .clr(rst));
  Adder #(.width(32)) adder_1 (.a(LRU_num_q), .b(32'h1), .out(adder_1_out));  // open: cin, cout
  Adder #(.width(32)) adder_2 (.a(LRU_num_2_q), .b(32'h1), .out(adder_2_out));  // open: cin, cout
  Adder #(.width(32)) adder_3 (.a(LRU_num_3_q), .b(32'h1), .out(adder_3_out));  // open: cin, cout
  Adder #(.width(32)) adder_4 (.a(LRU_num_4_q), .b(32'h1), .out(adder_4_out));  // open: cin, cout
  biggest biggest_1 (
    ._000(LRU_num_q), ._001(LRU_num_2_q), ._010(LRU_num_3_q), ._011(LRU_num_4_q), ._100(LRU_num_5_q),
    ._101(LRU_num_6_q), ._110(LRU_num_7_q), ._111(LRU_num_8_q), .\最大编号 (BiggestCode));  // open: 最大数据
  Adder #(.width(32)) adder_5 (.a(LRU_num_5_q), .b(32'h1), .out(adder_5_out));  // open: cin, cout
  Adder #(.width(32)) adder_6 (.a(LRU_num_6_q), .b(32'h1), .out(adder_6_out));  // open: cin, cout
  Adder #(.width(32)) adder_7 (.a(LRU_num_7_q), .b(32'h1), .out(adder_7_out));  // open: cin, cout
  Adder #(.width(32)) adder_8 (.a(LRU_num_8_q), .b(32'h1), .out(adder_8_out));  // open: cin, cout

  // Other names for the same wires on the sheet: 位置[2:0] = \命中位置 
endmodule

module biggest (
  input  [31:0] _000,
  input  [31:0] _001,
  input  [31:0] _010,
  input  [31:0] _011,
  input  [31:0] _100,
  input  [31:0] _101,
  input  [31:0] _110,
  input  [31:0] _111,
  output [31:0] \最大数据 ,
  output [2:0] \最大编号 
);

  wire comparator_1_lt, comparator_2_lt, comparator_3_lt, comparator_4_lt, comparator_5_lt, comparator_6_lt,
       comparator_7_lt;
  wire [2:0] multiplexer_5_out, multiplexer_6_out, multiplexer_7_out, multiplexer_8_out, multiplexer_11_out,
       multiplexer_12_out;
  wire [31:0] multiplexer_1_out, multiplexer_2_out, multiplexer_3_out, multiplexer_4_out, multiplexer_9_out,
       multiplexer_10_out;

  Multiplexer #(.width(32)) multiplexer_1 (
    .in0(_000), .in1(_001), .out(multiplexer_1_out), .sel(comparator_1_lt));  // open: en
  Comparator #(.width(32)) comparator_1 (.a(_000), .b(_001), .lt(comparator_1_lt));  // open: gt, eq
  Multiplexer #(.width(32)) multiplexer_2 (
    .in0(_010), .in1(_011), .out(multiplexer_2_out), .sel(comparator_2_lt));  // open: en
  Comparator #(.width(32)) comparator_2 (.a(_010), .b(_011), .lt(comparator_2_lt));  // open: gt, eq
  Multiplexer #(.width(32)) multiplexer_3 (
    .in0(_100), .in1(_101), .out(multiplexer_3_out), .sel(comparator_3_lt));  // open: en
  Comparator #(.width(32)) comparator_3 (.a(_100), .b(_101), .lt(comparator_3_lt));  // open: gt, eq
  Multiplexer #(.width(32)) multiplexer_4 (
    .in0(_110), .in1(_111), .out(multiplexer_4_out), .sel(comparator_4_lt));  // open: en
  Comparator #(.width(32)) comparator_4 (.a(_110), .b(_111), .lt(comparator_4_lt));  // open: gt, eq
  Multiplexer #(.width(3)) multiplexer_5 (
    .in0(3'b000), .in1(3'b001), .out(multiplexer_5_out), .sel(comparator_1_lt));  // open: en
  Multiplexer #(.width(3)) multiplexer_6 (
    .in0(3'b010), .in1(3'b011), .out(multiplexer_6_out), .sel(comparator_2_lt));  // open: en
  Multiplexer #(.width(3)) multiplexer_7 (
    .in0(3'b100), .in1(3'b101), .out(multiplexer_7_out), .sel(comparator_3_lt));  // open: en
  Multiplexer #(.width(3)) multiplexer_8 (
    .in0(3'b110), .in1(3'b111), .out(multiplexer_8_out), .sel(comparator_4_lt));  // open: en
  Comparator #(.width(32)) comparator_5 (
    .a(multiplexer_1_out), .b(multiplexer_2_out), .lt(comparator_5_lt));  // open: gt, eq
  Comparator #(.width(32)) comparator_6 (
    .a(multiplexer_3_out), .b(multiplexer_4_out), .lt(comparator_6_lt));  // open: gt, eq
  Multiplexer #(.width(32)) multiplexer_9 (
    .in0(multiplexer_1_out), .in1(multiplexer_2_out), .out(multiplexer_9_out), .sel(comparator_5_lt));  // open: en
  Multiplexer #(.width(32)) multiplexer_10 (
    .in0(multiplexer_3_out), .in1(multiplexer_4_out), .out(multiplexer_10_out), .sel(comparator_6_lt));  // open: en
  Multiplexer #(.width(3)) multiplexer_11 (
    .in0(multiplexer_5_out), .in1(multiplexer_6_out), .out(multiplexer_11_out), .sel(comparator_5_lt));  // open: en
  Multiplexer #(.width(3)) multiplexer_12 (
    .in0(multiplexer_7_out), .in1(multiplexer_8_out), .out(multiplexer_12_out), .sel(comparator_6_lt));  // open: en
  Comparator #(.width(32)) comparator_7 (
    .a(multiplexer_9_out), .b(multiplexer_10_out), .lt(comparator_7_lt));  // open: gt, eq
  Multiplexer #(.width(32)) multiplexer_13 (
    .in0(multiplexer_9_out), .in1(multiplexer_10_out), .out(\最大数据 ), .sel(comparator_7_lt));  // open: en
  Multiplexer #(.width(3)) multiplexer_14 (
    .in0(multiplexer_11_out), .in1(multiplexer_12_out), .out(\最大编号 ), .sel(comparator_7_lt));  // open: en
endmodule

module new_status (
  input  [1:0] old_status,
  input  [1:0] hit_jump,
  output [1:0] new_status
);

  wire [1:0] status_1_l_out, status_2_l_out;

  status status_1 (
    .high(old_status[1]), .low(old_status[0]), .in(1'b0), .h_out(status_1_l_out[1]), .l_out(status_1_l_out[0]));
  status status_2 (
    .high(old_status[1]), .low(old_status[0]), .in(1'b1), .h_out(status_2_l_out[1]), .l_out(status_2_l_out[0]));
  Multiplexer #(.select(2), .width(2)) multiplexer_1 (
    .in0(2'b01), .in1(2'b10), .in2(status_1_l_out), .in3(status_2_l_out), .out(new_status), .sel(hit_jump));  // open: en
endmodule

module status (
  input  high,
  input  low,
  input  in,
  output h_out,
  output l_out
);

  wire and_1_out, and_2_out, and_3_out;

  and and_1 (and_1_out, low, in);
  and and_2 (and_2_out, high, in);
  and and_3 (and_3_out, high, low);
  or or_1 (h_out, and_1_out, and_2_out, and_3_out);

  assign l_out = in;
endmodule

module decoder (
  input  [2:0] code,
  output k0,
  output k1,
  output k2,
  output k3,
  output k4,
  output k5,
  output k6,
  output k7
);

  wire not_1_out, not_2_out, not_3_out, not_4_out, not_5_out, not_6_out, not_7_out, not_8_out, not_9_out,
       not_10_out, not_11_out, not_12_out;

  not not_1 (not_1_out, code[2]);
  not not_2 (not_2_out, code[1]);
  not not_3 (not_3_out, code[0]);
  not not_4 (not_4_out, code[2]);
  not not_5 (not_5_out, code[1]);
  not not_6 (not_6_out, code[2]);
  not not_7 (not_7_out, code[0]);
  not not_8 (not_8_out, code[2]);
  not not_9 (not_9_out, code[1]);
  not not_10 (not_10_out, code[0]);
  not not_11 (not_11_out, code[1]);
  not not_12 (not_12_out, code[0]);
  and and_1 (k7, code[2], code[1], code[0]);
  and and_2 (k0, not_1_out, not_2_out, not_3_out);
  and and_3 (k1, not_4_out, not_5_out, code[0]);
  and and_4 (k2, not_6_out, code[1], not_7_out);
  and and_5 (k3, not_8_out, code[1], code[0]);
  and and_6 (k4, code[2], not_9_out, not_10_out);
  and and_7 (k5, code[2], not_11_out, code[0]);
  and and_8 (k6, code[2], code[1], not_12_out);
endmodule
