// Logisim project U201514714_张钧瑜_理想流水.circ as structural Verilog: 11 circuits, main circuit cpu
module cpu (
);

  wire ALU0, and_2_out, and_3_out, and_4_out, and_5_out, and_6_out, and_7_out, and_9_out, and_10_out,
       and_11_out, and_12_out, BRANCH, C1, C2, C3, C4, comparator_1_eq, comparator_2_eq, comparator_3_eq,
       comparator_4_eq, comparator_5_eq, decoder_1_out0, disp, equal, ex_mem_1_halt_2, ex_mem_1_memw_2,
       ex_mem_1_regwrite_2, ex_mem_1_syscall_2, greater, halt, halt0, id_ex_1_halt_2, id_ex_1_memw_2,
       id_ex_1_regwrite_2, id_ex_1_syscall, JUMP, mem_wb_1_regwrite_2, nand_1_out, not_1_out, not_2_out,
       not_4_out, not_5_out, or_1_out, register_1_q, RST, srlv, success, SYSCALL, SYSCALLbegin,
       \控制器_1_branch , \控制器_1_ext_sign , \控制器_1_ext_slt , \控制器_1_jump , \控制器_1_memw , \控制器_1_regwrite ,
       \比较结果 ;
  wire [1:0] counter_1_q, ex_mem_1_regdst_2, ex_mem_1_rf_w_2, id_ex_1_aluscr_2, id_ex_1_regdst_2,
       id_ex_1_rf_w_2, mem_wb_1_regdst_2, mem_wb_1_rf_w_2, \控制器_1_aluscr , \控制器_1_regdst , \控制器_1_rf_w ,
       \控制器_1_rfr1 ;
  wire [3:0] id_ex_1_aluop_2, \控制器_1_aluop ;
  wire [4:0] multiplexer_1_out, multiplexer_3_out, multiplexer_4_out, \解码器_1__11_15位_rd___win_寄存器堆写入寄存器号 ,
       \解码器_1__16_20位_rt_____win_寄存器堆写入寄存器号 , \解码器_1__21_25位_rs , \解码器_1_移位sa ;
  wire [9:0] ex_mem_1_rd_rt_2, id_ex_1_rd_rt_2, mem_wb_1_rd_rt_2;
  wire [15:0] bit_extender_1_out, multiplexer_2_out, \总周期数 , \无条件分支指令数 , \有条件分支成功跳转 , \有条件分支指令数 ,
       \解码器_1__0_15位符号扩展输入 ;
  wire [19:0] \控制指令 ;
  wire [23:0] ex_mem_1_alu24_2;
  wire [25:0] shifter_1_out, \无条件转移 ;
  wire [31:0] adder_1_out, adder_2_out, ex_mem_1_aluresult_2, ex_mem_1_jumpto, ex_mem_1_pc_4_2,
       ex_mem_1_r2_2, id_ex_1_ext_2, id_ex_1_pc_4_2, id_ex_1_r1, id_ex_1_r2, \id_ex_1_无条件转移 , if_id_1_ir,
       if_id_1_pc_4_2, mem_wb_1_aluresult_2, mem_wb_1_data_2, mem_wb_1_pc_4_2, mips_ram_1_p8,
       multiplexer_5_out, multiplexer_6_out, multiplexer_7_out, multiplexer_8_out, multiplexer_9_out,
       multiplexer_10_out, multiplexer_11_out, PC_q, RFR1, RFR2, rom_1_data, shifter_2_out, SyscallOut,
       \寄存器堆_1_rf_r2 , \扩展器_1_输出32位 ;
  wire [31:1] alu_1_result;

  Button \u_总复位  (.out(RST));
  not not_1 (not_1_out, halt0);
  Register #(.width(32)) PC (.D(ex_mem_1_jumpto), .en(not_1_out), .Q(PC_q), .clk(C1), .clr(RST));
  Hex_Digit_Display hex_digit_display_1 (.value(SyscallOut[27:24]));  // open: dp
  Hex_Digit_Display hex_digit_display_2 (.value(SyscallOut[31:28]));  // open: dp
  Hex_Digit_Display hex_digit_display_3 (.value(SyscallOut[19:16]));  // open: dp
  Hex_Digit_Display hex_digit_display_4 (.value(SyscallOut[23:20]));  // open: dp
  Adder #(.width(32)) adder_1 (.a(32'h4), .b(PC_q), .out(adder_1_out));  // open: cin, cout
  Hex_Digit_Display hex_digit_display_5 (.value(SyscallOut[11:8]));  // open: dp
  Hex_Digit_Display hex_digit_display_6 (.value(SyscallOut[15:12]));  // open: dp
  IF_ID if_id_1 (.\指令 (rom_1_data), .PC_4(adder_1_out), .IR(if_id_1_ir), .PC_4_2(if_id_1_pc_4_2), .rst(RST), .clk(C1));
  ROM #(.addrWidth(10), .dataWidth(32)) rom_1 (.addr(PC_q[11:2]), .data(rom_1_data));  // open: sel
  Hex_Digit_Display hex_digit_display_7 (.value(SyscallOut[3:0]));  // open: dp
  Hex_Digit_Display hex_digit_display_8 (.value(SyscallOut[7:4]));  // open: dp
  Shifter #(.width(26)) shifter_1 (.in(\无条件转移 ), .\dist (5'b00010), .out(shifter_1_out));
  \解码器  \u_解码器_1  (
    .\指令 (if_id_1_ir), .\_21_25位_rs (\解码器_1__21_25位_rs ),
    .\_16_20位_rt_____Win_寄存器堆写入寄存器号 (\解码器_1__16_20位_rt_____win_寄存器堆写入寄存器号 ),
    .\_0_15位符号扩展输入 (\解码器_1__0_15位符号扩展输入 ),
    .\_11_15位_rd___Win_寄存器堆写入寄存器号 (\解码器_1__11_15位_rd___win_寄存器堆写入寄存器号 ), .\_0_25位无条件转移地址 (\无条件转移 ),
    .\移位sa (\解码器_1_移位sa ));
  assign bit_extender_1_out = {{11{1'b0}}, \解码器_1_移位sa };  // Bit_Extender bit_extender_1
  \控制器  \u_控制器_1  (
    .MemW(\控制器_1_memw ), .RegWrite(\控制器_1_regwrite ), .\输入指令 (if_id_1_ir), .regdst(\控制器_1_regdst ),
    .halt(SYSCALLbegin), .RFR1(\控制器_1_rfr1 ), .ext_sign(\控制器_1_ext_sign ), .aluscr(\控制器_1_aluscr ),
    .ext_slt(\控制器_1_ext_slt ), .RF_W(\控制器_1_rf_w ), .aluop(\控制器_1_aluop ), .jump(\控制器_1_jump ),
    .branch(\控制器_1_branch ), .out_13(\控制指令 ));  // open: disp
  Multiplexer #(.width(5), .enable("false")) multiplexer_1 (
    .in0(\解码器_1__16_20位_rt_____win_寄存器堆写入寄存器号 ), .in1(5'b00100), .out(multiplexer_1_out), .sel(SYSCALLbegin));
  Multiplexer #(.width(16), .enable("false")) multiplexer_2 (
    .in0(bit_extender_1_out), .in1(\解码器_1__0_15位符号扩展输入 ), .out(multiplexer_2_out), .sel(\控制器_1_ext_slt ));
  // Probe on \总周期数 
  // Probe on \无条件分支指令数 
  // Probe on \有条件分支指令数 
  // Probe on \有条件分支成功跳转 
  Multiplexer #(.select(2), .width(5), .enable("false")) multiplexer_3 (
    .in0(\解码器_1__21_25位_rs ), .in1(\解码器_1__16_20位_rt_____win_寄存器堆写入寄存器号 ), .in2(5'b00010), .in3({5{1'b0}}),
    .out(multiplexer_3_out), .sel(\控制器_1_rfr1 ));
  \扩展器  \u_扩展器_1  (.\输入16位 (multiplexer_2_out), .\输出32位 (\扩展器_1_输出32位 ), .\_0为0拓展_1为符号拓展 (\控制器_1_ext_sign ));
  Multiplexer #(.select(2), .width(5), .enable("false")) multiplexer_4 (
    .in0(mem_wb_1_rd_rt_2[9:5]), .in1(mem_wb_1_rd_rt_2[4:0]), .in2({5{1'b1}}), .in3({5{1'b0}}),
    .out(multiplexer_4_out), .sel(mem_wb_1_regdst_2));
  \寄存器堆  \u_寄存器堆_1  (
    .Din(multiplexer_10_out), .clk(C1), .RegWrite(mem_wb_1_regwrite_2), .W(multiplexer_4_out), .RF_R1(RFR1),
    .RF_R2(\寄存器堆_1_rf_r2 ), .R2(multiplexer_1_out), .R1(multiplexer_3_out));
  Counter #(.width(2), .max('h3)) counter_1 (.Q(counter_1_q));  // open: load, D, count, carry, clk, clr
  Clock clock_1 (.out(C1));
  ID_EX id_ex_1 (
    .\无条件转移计算 ({if_id_1_pc_4_2[31:28], 2'b00, shifter_1_out}), .branch(\控制器_1_branch ),
    .PC_4(if_id_1_pc_4_2), .junp(\控制器_1_jump ), .memW(\控制器_1_memw ), .RF_R1(RFR1), .aluop(\控制器_1_aluop ),
    .RF_R2(\寄存器堆_1_rf_r2 ), .rf_w(\控制器_1_rf_w ), .ext(\扩展器_1_输出32位 ), .aluscr(\控制器_1_aluscr ),
    .\无条件转移 (\id_ex_1_无条件转移 ), .BRANCH_2(BRANCH), .PC_4_2(id_ex_1_pc_4_2), .JUMP(JUMP),
    .MEMW_2(id_ex_1_memw_2), .R1(id_ex_1_r1), .ALUOP_2(id_ex_1_aluop_2), .R2(id_ex_1_r2),
    .RF_W_2(id_ex_1_rf_w_2), .ext_2(id_ex_1_ext_2), .ALUSCR_2(id_ex_1_aluscr_2), .rst(RST), .clk(C1),
    .regwrite(\控制器_1_regwrite ), .REGWRITE_2(id_ex_1_regwrite_2), .regdst(\控制器_1_regdst ),
    .REGDST_2(id_ex_1_regdst_2), .RD_RT_2(id_ex_1_rd_rt_2),
    .rd_rt({\解码器_1__11_15位_rd___win_寄存器堆写入寄存器号 , \解码器_1__16_20位_rt_____win_寄存器堆写入寄存器号 }),
    .systemcall(SYSCALLbegin), .SYSCALL(id_ex_1_syscall), .halt(halt), .halt_2(id_ex_1_halt_2));
  Decoder #(.select(2)) decoder_1 (
    .out0(decoder_1_out0), .out1(C2), .out2(C3), .out3(C4), .sel(counter_1_q), .en(1'b1));
  Shifter #(.width(32)) shifter_2 (.in(id_ex_1_ext_2), .\dist (5'b00010), .out(shifter_2_out));
  Adder #(.width(32)) adder_2 (.a(id_ex_1_pc_4_2), .b(shifter_2_out), .out(adder_2_out));  // open: cin, cout
  Multiplexer #(.width(32), .enable("false")) multiplexer_5 (
    .in0(id_ex_1_r1), .in1(id_ex_1_r2), .out(multiplexer_5_out), .sel(srlv));
  Multiplexer #(.select(2), .width(32), .enable("false")) multiplexer_6 (
    .in0(id_ex_1_r2), .in1(id_ex_1_ext_2), .in2({32{1'b0}}), .in3(id_ex_1_r1), .out(multiplexer_6_out),
    .sel(id_ex_1_aluscr_2));
  and and_1 (success, \比较结果 , BRANCH);
  alu alu_1 (
    .X(multiplexer_5_out), .Y(multiplexer_6_out), .AluOP(id_ex_1_aluop_2), .Equal(equal),
    .Result({alu_1_result, ALU0}));  // open: Signed_Overflow, UnSigned_Overflow, Result_2
  Multiplexer #(.width(32), .enable("false")) multiplexer_7 (
    .in0(id_ex_1_pc_4_2), .in1(adder_2_out), .out(multiplexer_7_out), .sel(success));
  Multiplexer #(.width(32), .enable("false")) multiplexer_8 (
    .in0(multiplexer_7_out), .in1(\id_ex_1_无条件转移 ), .out(multiplexer_8_out), .sel(JUMP));
  Multiplexer #(.width(32), .enable("false")) multiplexer_9 (
    .in0(multiplexer_8_out), .in1(RFR1), .out(multiplexer_9_out), .sel(and_2_out));
  and and_2 (and_2_out, BRANCH, JUMP);
  EX_MEM ex_mem_1 (
    .jump_to(multiplexer_9_out), .PC_4(id_ex_1_pc_4_2), .aluresult({alu_1_result, ALU0}),
    .alu24(alu_1_result[25:2]), .memw(id_ex_1_memw_2), .rf_w(id_ex_1_rf_w_2), .r2(id_ex_1_r2),
    .JUMPTO(ex_mem_1_jumpto), .PC_4_2(ex_mem_1_pc_4_2), .ALURESULT_2(ex_mem_1_aluresult_2),
    .ALU24_2(ex_mem_1_alu24_2), .MEMW_2(ex_mem_1_memw_2), .RF_W_2(ex_mem_1_rf_w_2), .R2_2(ex_mem_1_r2_2),
    .rst(RST), .clk(C1), .regwrite(id_ex_1_regwrite_2), .REGWRITE_2(ex_mem_1_regwrite_2),
    .rd_rt(id_ex_1_rd_rt_2), .RD_RT_2(ex_mem_1_rd_rt_2), .regdst(id_ex_1_regdst_2),
    .REGDST_2(ex_mem_1_regdst_2), .syscall(id_ex_1_syscall), .SYSCALL_2(ex_mem_1_syscall_2),
    .halt(id_ex_1_halt_2), .halt_2(ex_mem_1_halt_2));
  // Probe on ex_mem_1_alu24_2
  MEM_WB mem_wb_1 (
    .PC_4(ex_mem_1_pc_4_2), .aluresult(ex_mem_1_aluresult_2), .rf_w(ex_mem_1_rf_w_2), .data(mips_ram_1_p8),
    .PC_4_2(mem_wb_1_pc_4_2), .ALURESULT_2(mem_wb_1_aluresult_2), .RF_W_2(mem_wb_1_rf_w_2),
    .DATA_2(mem_wb_1_data_2), .rst(RST), .clk(C1), .REGWRITE_2(mem_wb_1_regwrite_2),
    .regwrite(ex_mem_1_regwrite_2), .rd_rt(ex_mem_1_rd_rt_2), .RD_RT_2(mem_wb_1_rd_rt_2),
    .regdst(ex_mem_1_regdst_2), .REGDST_2(mem_wb_1_regdst_2), .sysycall(ex_mem_1_syscall_2),
    .SYSCALL(SYSCALL), .halt(ex_mem_1_halt_2), .halt_2(halt0));
  // MIPS_RAM mips_ram_1: pin names not known; wires that end beside it: ex_mem_1_alu24_2, ex_mem_1_r2_2, ex_mem_1_memw_2, 4'b1111, C1, 1'b1, RST, mips_ram_1_p8
  Multiplexer #(.select(2), .width(32), .enable("false")) multiplexer_10 (
    .in0(mem_wb_1_aluresult_2), .in1(mem_wb_1_pc_4_2), .in2(mem_wb_1_data_2), .in3({32{1'b0}}),
    .out(multiplexer_10_out), .sel(mem_wb_1_rf_w_2));
  Counter #(.width(16), .max('hffff)) counter_2 (.Q(\总周期数 ), .clk(or_1_out), .clr(RST));  // open: load, D, count, carry
  or or_1 (or_1_out, and_3_out, register_1_q);
  and and_3 (and_3_out, C1, nand_1_out);
  nand nand_1 (nand_1_out, halt0, SYSCALL);
  Multiplexer #(.width(32)) multiplexer_11 (.in1(RFR2), .out(multiplexer_11_out), .sel(disp), .en(1'b1));  // open: in0
  and and_4 (and_4_out, halt0, SYSCALL);
  Register #(.width(1)) register_1 (.D(and_4_out), .Q(register_1_q), .clk(C1), .clr(RST));  // open: en
  Register #(.width(4)) register_2 (.D(multiplexer_11_out[3:0]), .Q(SyscallOut[3:0]), .clk(C1), .clr(RST));  // open: en
  Register #(.width(4)) register_3 (.D(multiplexer_11_out[7:4]), .Q(SyscallOut[7:4]), .clk(C1), .clr(RST));  // open: en
  Register #(.width(4)) register_4 (
    .D(multiplexer_11_out[11:8]), .Q(SyscallOut[11:8]), .clk(C1), .clr(RST));  // open: en
  Register #(.width(4)) register_5 (
    .D(multiplexer_11_out[15:12]), .Q(SyscallOut[15:12]), .clk(C1), .clr(RST));  // open: en
  Register #(.width(4)) register_6 (
    .D(multiplexer_11_out[19:16]), .Q(SyscallOut[19:16]), .clk(C1), .clr(RST));  // open: en
  Register #(.width(4)) register_7 (
    .D(multiplexer_11_out[23:20]), .Q(SyscallOut[23:20]), .clk(C1), .clr(RST));  // open: en
  Register #(.width(4)) register_8 (
    .D(multiplexer_11_out[27:24]), .Q(SyscallOut[27:24]), .clk(C1), .clr(RST));  // open: en
  Register #(.width(4)) register_9 (
    .D(multiplexer_11_out[31:28]), .Q(SyscallOut[31:28]), .clk(C1), .clr(RST));  // open: en
  not not_2 (not_2_out, JUMP);
  and and_5 (and_5_out, not_2_out, BRANCH);
  Comparator #(.width(1)) comparator_1 (.a(JUMP), .b(1'b1), .eq(comparator_1_eq));  // open: gt, lt
  Counter #(.width(16), .max('hffff)) counter_3 (
    .Q(\有条件分支指令数 ), .clk(and_6_out), .clr(RST));  // open: load, D, count, carry
  and and_6 (and_6_out, and_5_out, C1);
  Counter #(.width(16), .max('hffff)) counter_4 (
    .Q(\无条件分支指令数 ), .clk(and_7_out), .clr(RST));  // open: load, D, count, carry
  and and_7 (and_7_out, comparator_1_eq, C1);
  not not_3 (greater, ALU0);
  Comparator #(.width(32), .mode("unsigned")) comparator_2 (.a(RFR1), .b(32'ha), .eq(comparator_2_eq));  // open: gt, lt
  and and_8 (halt, comparator_2_eq, SYSCALLbegin);
  not not_4 (not_4_out, equal);
  Comparator #(.width(20), .mode("unsigned")) comparator_3 (
    .a(\控制指令 ), .b(20'hb19), .eq(comparator_3_eq));  // open: gt, lt
  Comparator #(.width(20), .mode("unsigned")) comparator_4 (
    .a(\控制指令 ), .b(20'hb1d), .eq(comparator_4_eq));  // open: gt, lt
  Comparator #(.width(20), .mode("unsigned")) comparator_5 (
    .a(\控制指令 ), .b(20'h8b19), .eq(comparator_5_eq));  // open: gt, lt
  Counter #(.width(16), .max('hffff)) counter_5 (
    .Q(\有条件分支成功跳转 ), .clk(and_9_out), .clr(RST));  // open: load, D, count, carry
  and and_9 (and_9_out, success, C1);
  and and_10 (and_10_out, equal, comparator_3_eq);
  and and_11 (and_11_out, not_4_out, comparator_4_eq);
  and and_12 (and_12_out, comparator_5_eq, greater);
  not not_5 (not_5_out, halt);
  or or_2 (\比较结果 , and_10_out, and_11_out, and_12_out);
  Comparator #(.width(20), .mode("unsigned")) comparator_6 (.a(\控制指令 ), .b(20'hc240), .eq(srlv));  // open: gt, lt
  and and_13 (disp, not_5_out, SYSCALL);

  // Notes on the sheet:
  //   取指令周期IF
  //   数码管输出应该用寄存器锁存，否则显示数据只能一闪而过
  //   可以通过项目增加Logisim库的方式将前几次实验完成的电路作为子电路引入到本电路中使用
  //   contents of rom_1 (hex, n*v repeats v):
  //   20100000 20110000 20120000 20130000 36100000 36310001 36520002 36730003 ae100000 ae110004 ae120008
  //   ae13000c 2002000a 20110000 20120000 20130000 c
  //   数码管输出
  //   无条件转移 左移两位合并高四位
  //   指令译码/读寄存器周期
  //   总复位信号应将除ROM以外所有存储组件全部清零
  //   时钟
  //   执行/有效地址计算周期
  //   存储器访问/分支完成周期
  //   WB
  //   显示模块
  //   syscall
  //   BEQ、BGEZ及SRLV
  //   BEQ
  //   BNE
  //   BGEZ
endmodule

// EXT
module \扩展器  (
  input  [15:0] \输入16位 ,
  input  \_0为0拓展_1为符号拓展 ,
  output [31:0] \输出32位 
);

  wire [31:0] bit_extender_1_out, bit_extender_2_out;

  assign bit_extender_1_out = {{16{1'b0}}, \输入16位 };  // Bit_Extender bit_extender_1
  assign bit_extender_2_out = {{16{\输入16位 [15]}}, \输入16位 };  // Bit_Extender bit_extender_2
  Multiplexer #(.width(32), .enable("false")) multiplexer_1 (
    .in0(bit_extender_1_out), .in1(bit_extender_2_out), .out(\输出32位 ), .sel(\_0为0拓展_1为符号拓展 ));

  // Notes on the sheet:
  //   extend扩展器
  //   0扩展
  //   符号扩展
  //   sign标志为1 进行符号扩展；否则进行0扩展
endmodule

module \解码器  (
  input  [31:0] \指令 ,
  output [4:0] \_21_25位_rs ,
  output [4:0] \_16_20位_rt_____Win_寄存器堆写入寄存器号 ,
  output [15:0] \_0_15位符号扩展输入 ,
  output [4:0] \_11_15位_rd___Win_寄存器堆写入寄存器号 ,
  output [25:0] \_0_25位无条件转移地址 ,
  output [4:0] \移位sa 
);


  assign \_0_15位符号扩展输入  = \指令 [15:0];
  assign \_0_25位无条件转移地址  = \指令 [25:0];
  assign \_11_15位_rd___Win_寄存器堆写入寄存器号  = \指令 [15:11];
  assign \_16_20位_rt_____Win_寄存器堆写入寄存器号  = \指令 [20:16];
  assign \_21_25位_rs  = \指令 [25:21];
  assign \移位sa  = \指令 [10:6];

  // Notes on the sheet:
  //   Decorder解码器
endmodule

// IR
module \指令存储器  (
  input  [9:0] \PC_2_11位_指令地址 ,
  output [31:0] \_32位指令 
);

  ROM #(.addrWidth(10), .dataWidth(32)) rom_1 (.addr(\PC_2_11位_指令地址 ), .data(\_32位指令 ), .sel(1'b1));

  // Notes on the sheet:
  //   指令存储器
  //   contents of rom_1 (hex, n*v repeats v):
  //   20100000 20110000 20120000 20130000 36100000 36310001 36520002 36730003 ae100000 ae110004 ae120008
  //   ae13000c 2002000a 20110000 20120000 20130000 c
endmodule

module \控制器  (
  input  [31:0] \输入指令 ,
  output MemW,
  output ext_sign,
  output [1:0] regdst,
  output RegWrite,
  output [1:0] RFR1,
  output ext_slt,
  output [1:0] aluscr,
  output halt,
  output disp,
  output [1:0] RF_W,
  output jump,
  output [19:0] out_13,
  output [3:0] aluop,
  output branch
);

  wire and_1_out, and_2_out, and_3_out, and_4_out, and_5_out, and_6_out, and_7_out, and_8_out, and_9_out,
       and_10_out, and_11_out, and_12_out, and_13_out, and_14_out, and_15_out, comparator_1_eq,
       comparator_2_eq, comparator_3_eq, comparator_4_eq, comparator_5_eq, comparator_6_eq, comparator_7_eq,
       comparator_8_eq, comparator_9_eq, comparator_10_eq, comparator_11_eq, comparator_12_eq,
       comparator_13_eq, comparator_14_eq, comparator_15_eq, comparator_16_eq, comparator_17_eq,
       comparator_18_eq, comparator_19_eq, comparator_20_eq, comparator_21_eq, comparator_22_eq,
       comparator_23_eq, comparator_24_eq, comparator_25_eq, comparator_26_eq, comparator_27_eq,
       comparator_28_eq, comparator_29_eq;
  wire [19:0] add, addi, addiu, addu, \and , andi, beq, bgez, bne, j, jl, jr, lh, lw, \nor , \or , ori, sll,
       slt, slti, sltu, sra, srl, srlv, sub, sw, syscall, \xor ;

  // Probe on {out_13[19:16], aluscr, out_13[13:12], aluop, MemW, out_13[6], halt, ext_sign, ext_slt, disp, jump, branch}
  Comparator #(.width(6), .mode("unsigned")) comparator_1 (
    .a(\输入指令 [31:26]), .b(6'b001000), .eq(comparator_1_eq));  // open: gt, lt
  Comparator #(.width(6), .mode("unsigned")) comparator_2 (
    .a(\输入指令 [31:26]), .b(6'b001001), .eq(comparator_2_eq));  // open: gt, lt
  Comparator #(.width(6), .mode("unsigned")) comparator_3 (
    .a(\输入指令 [31:26]), .b(6'b001100), .eq(comparator_3_eq));  // open: gt, lt
  Comparator #(.width(6), .mode("unsigned")) comparator_4 (
    .a(\输入指令 [31:26]), .b(6'b001101), .eq(comparator_4_eq));  // open: gt, lt
  Comparator #(.width(6), .mode("unsigned")) comparator_5 (
    .a(\输入指令 [31:26]), .b(6'b100011), .eq(comparator_5_eq));  // open: gt, lt
  Comparator #(.width(6), .mode("unsigned")) comparator_6 (
    .a(\输入指令 [31:26]), .b(6'b101011), .eq(comparator_6_eq));  // open: gt, lt
  Comparator #(.width(6), .mode("unsigned")) comparator_7 (
    .a(\输入指令 [31:26]), .b(6'b000100), .eq(comparator_7_eq));  // open: gt, lt
  Comparator #(.width(6), .mode("unsigned")) comparator_8 (
    .a(\输入指令 [31:26]), .b(6'b000101), .eq(comparator_8_eq));  // open: gt, lt
  Comparator #(.width(6), .mode("unsigned")) comparator_9 (
    .a(\输入指令 [31:26]), .b(6'b001010), .eq(comparator_9_eq));  // open: gt, lt
  Comparator #(.width(6), .mode("unsigned")) comparator_10 (
    .a(\输入指令 [31:26]), .b(6'b000010), .eq(comparator_10_eq));  // open: gt, lt
  Comparator #(.width(6), .mode("unsigned")) comparator_11 (
    .a(\输入指令 [31:26]), .b(6'b000011), .eq(comparator_11_eq));  // open: gt, lt
  Comparator #(.width(6), .mode("unsigned")) comparator_12 (
    .a(\输入指令 [31:26]), .b(6'b100001), .eq(comparator_12_eq));  // open: gt, lt
  Comparator #(.width(6), .mode("unsigned")) comparator_13 (
    .a(\输入指令 [31:26]), .b(6'b000001), .eq(comparator_13_eq));  // open: gt, lt
  Comparator #(.width(6), .mode("unsigned")) comparator_14 (
    .a(\输入指令 [31:26]), .b({6{1'b0}}), .eq(comparator_14_eq));  // open: gt, lt
  // Probe on {out_13[19:16], aluscr, out_13[13:12], aluop, MemW, out_13[6], halt, ext_sign, ext_slt, disp, jump, branch}
  Multiplexer #(.width(20), .enable("false")) multiplexer_1 (
    .in0({20{1'b0}}), .in1(20'h44558), .out(addi), .sel(comparator_1_eq));
  Multiplexer #(.width(20), .enable("false")) multiplexer_2 (
    .in0({20{1'b0}}), .in1(20'h44558), .out(addiu), .sel(comparator_2_eq));
  Multiplexer #(.width(20), .enable("false")) multiplexer_3 (
    .in0({20{1'b0}}), .in1(20'h44748), .out(andi), .sel(comparator_3_eq));
  Multiplexer #(.width(20), .enable("false")) multiplexer_4 (
    .in0({20{1'b0}}), .in1(20'h44848), .out(ori), .sel(comparator_4_eq));
  Multiplexer #(.width(20), .enable("false")) multiplexer_5 (
    .in0({20{1'b0}}), .in1(20'h46558), .out(lw), .sel(comparator_5_eq));
  Multiplexer #(.width(20), .enable("false")) multiplexer_6 (
    .in0({20{1'b0}}), .in1(20'h4598), .out(sw), .sel(comparator_6_eq));
  Multiplexer #(.width(20), .enable("false")) multiplexer_7 (
    .in0({20{1'b0}}), .in1(20'hb19), .out(beq), .sel(comparator_7_eq));
  Multiplexer #(.width(20), .enable("false")) multiplexer_8 (
    .in0({20{1'b0}}), .in1(20'hb1d), .out(bne), .sel(comparator_8_eq));
  Multiplexer #(.width(20), .enable("false")) multiplexer_9 (
    .in0({20{1'b0}}), .in1(20'h4b58), .out(slti), .sel(comparator_9_eq));
  Multiplexer #(.width(20), .enable("false")) multiplexer_10 (
    .in0({20{1'b0}}), .in1(20'h2), .out(j), .sel(comparator_10_eq));
  Multiplexer #(.width(20), .enable("false")) multiplexer_11 (
    .in0({20{1'b0}}), .in1(20'h81042), .out(jl), .sel(comparator_11_eq));
  Multiplexer #(.width(20), .enable("false")) multiplexer_12 (
    .in0({20{1'b0}}), .in1(20'h46558), .out(lh), .sel(comparator_12_eq));
  Multiplexer #(.width(20), .enable("false")) multiplexer_13 (
    .in0({20{1'b0}}), .in1(20'h8b19), .out(bgez), .sel(comparator_13_eq));
  // Probe on \输入指令 [31:26]
  // Probe on \输入指令 
  // Probe on \输入指令 [25:21]
  Comparator #(.width(6), .mode("unsigned")) comparator_15 (
    .a(\输入指令 [5:0]), .b(6'b000011), .eq(comparator_15_eq));  // open: gt, lt
  // Probe on \输入指令 [20:16]
  Comparator #(.width(6), .mode("unsigned")) comparator_16 (
    .a(\输入指令 [5:0]), .b(6'b100000), .eq(comparator_16_eq));  // open: gt, lt
  Comparator #(.width(6), .mode("unsigned")) comparator_17 (
    .a(\输入指令 [5:0]), .b(6'b100001), .eq(comparator_17_eq));  // open: gt, lt
  Comparator #(.width(6), .mode("unsigned")) comparator_18 (
    .a(\输入指令 [5:0]), .b(6'b100100), .eq(comparator_18_eq));  // open: gt, lt
  Comparator #(.width(6), .mode("unsigned")) comparator_19 (
    .a(\输入指令 [5:0]), .b({6{1'b0}}), .eq(comparator_19_eq));  // open: gt, lt
  Comparator #(.width(6), .mode("unsigned")) comparator_20 (
    .a(\输入指令 [5:0]), .b(6'b000010), .eq(comparator_20_eq));  // open: gt, lt
  Comparator #(.width(6), .mode("unsigned")) comparator_21 (
    .a(\输入指令 [5:0]), .b(6'b100010), .eq(comparator_21_eq));  // open: gt, lt
  Comparator #(.width(6), .mode("unsigned")) comparator_22 (
    .a(\输入指令 [5:0]), .b(6'b100101), .eq(comparator_22_eq));  // open: gt, lt
  Comparator #(.width(6), .mode("unsigned")) comparator_23 (
    .a(\输入指令 [5:0]), .b(6'b100111), .eq(comparator_23_eq));  // open: gt, lt
  Comparator #(.width(6), .mode("unsigned")) comparator_24 (
    .a(\输入指令 [5:0]), .b(6'b101010), .eq(comparator_24_eq));  // open: gt, lt
  Comparator #(.width(6), .mode("unsigned")) comparator_25 (
    .a(\输入指令 [5:0]), .b(6'b101011), .eq(comparator_25_eq));  // open: gt, lt
  Comparator #(.width(6), .mode("unsigned")) comparator_26 (
    .a(\输入指令 [5:0]), .b(6'b001000), .eq(comparator_26_eq));  // open: gt, lt
  Comparator #(.width(6), .mode("unsigned")) comparator_27 (
    .a(\输入指令 [5:0]), .b(6'b000110), .eq(comparator_27_eq));  // open: gt, lt
  Comparator #(.width(6), .mode("unsigned")) comparator_28 (
    .a(\输入指令 [5:0]), .b(6'b100110), .eq(comparator_28_eq));  // open: gt, lt
  Comparator #(.width(6), .mode("unsigned")) comparator_29 (
    .a(\输入指令 [5:0]), .b(6'b001100), .eq(comparator_29_eq));  // open: gt, lt
  // Probe on \输入指令 [10:6]
  // Probe on \输入指令 [15:11]
  and and_1 (and_1_out, comparator_16_eq, comparator_14_eq);
  Multiplexer #(.width(20), .enable("false")) multiplexer_14 (
    .in0({20{1'b0}}), .in1(20'h540), .out(add), .sel(and_1_out));
  and and_2 (and_2_out, comparator_17_eq, comparator_14_eq);
  Multiplexer #(.width(20), .enable("false")) multiplexer_15 (
    .in0({20{1'b0}}), .in1(20'h540), .out(addu), .sel(and_2_out));
  and and_3 (and_3_out, comparator_18_eq, comparator_14_eq);
  Multiplexer #(.width(20), .enable("false")) multiplexer_16 (
    .in0({20{1'b0}}), .in1(20'h740), .out(\and ), .sel(and_3_out));
  and and_4 (and_4_out, comparator_19_eq, comparator_14_eq);
  Multiplexer #(.width(20), .enable("false")) multiplexer_17 (
    .in0({20{1'b0}}), .in1(20'h14040), .out(sll), .sel(and_4_out));
  and and_5 (and_5_out, comparator_15_eq, comparator_14_eq);
  Multiplexer #(.width(20), .enable("false")) multiplexer_18 (
    .in0({20{1'b0}}), .in1(20'h14140), .out(sra), .sel(and_5_out));
  and and_6 (and_6_out, comparator_20_eq, comparator_14_eq);
  Multiplexer #(.width(20), .enable("false")) multiplexer_19 (
    .in0({20{1'b0}}), .in1(20'h14240), .out(srl), .sel(and_6_out));
  and and_7 (and_7_out, comparator_21_eq, comparator_14_eq);
  Multiplexer #(.width(20), .enable("false")) multiplexer_20 (
    .in0({20{1'b0}}), .in1(20'h640), .out(sub), .sel(and_7_out));
  and and_8 (and_8_out, comparator_22_eq, comparator_14_eq);
  Multiplexer #(.width(20), .enable("false")) multiplexer_21 (
    .in0({20{1'b0}}), .in1(20'h840), .out(\or ), .sel(and_8_out));
  and and_9 (and_9_out, comparator_23_eq, comparator_14_eq);
  Multiplexer #(.width(20), .enable("false")) multiplexer_22 (
    .in0({20{1'b0}}), .in1(20'ha40), .out(\nor ), .sel(and_9_out));
  and and_10 (and_10_out, comparator_24_eq, comparator_14_eq);
  Multiplexer #(.width(20), .enable("false")) multiplexer_23 (
    .in0({20{1'b0}}), .in1(20'hb40), .out(slt), .sel(and_10_out));
  and and_11 (and_11_out, comparator_25_eq, comparator_14_eq);
  Multiplexer #(.width(20), .enable("false")) multiplexer_24 (
    .in0({20{1'b0}}), .in1(20'hc40), .out(sltu), .sel(and_11_out));
  and and_12 (and_12_out, comparator_26_eq, comparator_14_eq);
  Multiplexer #(.width(20), .enable("false")) multiplexer_25 (
    .in0({20{1'b0}}), .in1(20'h3), .out(jr), .sel(and_12_out));
  and and_13 (and_13_out, comparator_27_eq, comparator_14_eq);
  Multiplexer #(.width(20), .enable("false")) multiplexer_26 (
    .in0({20{1'b0}}), .in1(20'hc240), .out(srlv), .sel(and_13_out));
  and and_14 (and_14_out, comparator_28_eq, comparator_14_eq);
  Multiplexer #(.width(20), .enable("false")) multiplexer_27 (
    .in0({20{1'b0}}), .in1(20'h940), .out(\xor ), .sel(and_14_out));
  and and_15 (and_15_out, comparator_29_eq, comparator_14_eq);
  Multiplexer #(.width(20), .enable("false")) multiplexer_28 (
    .in0({20{1'b0}}), .in1(20'h20024), .out(syscall), .sel(and_15_out));
  // Probe on \输入指令 [5:0]
  assign {out_13[19:16], aluscr, out_13[13:12], aluop, MemW, out_13[6], halt, ext_sign, ext_slt, disp, jump, branch} = addi | addiu | andi | ori | lw | sw | beq | bne | slti | j | jl | lh | bgez | add | addu | \and  | sll | sra | srl | sub | \or  | \nor  | slt | sltu | jr | srlv | \xor  | syscall;  // OR_Gate or_1, 20 bits wide

  assign {out_13[15:14], out_13[11:7], out_13[5:0]} = {aluscr, aluop, MemW, halt, ext_sign, ext_slt, disp, jump, branch};
  assign regdst = out_13[19:18];
  assign RegWrite = out_13[6];
  assign RF_W = out_13[13:12];
  assign RFR1 = out_13[17:16];

  // Other names for the same wires on the sheet: 控制信号[19:0] = {out_13[19:16], aluscr, out_13[13:12], aluop, MemW, out_13[6], halt, ext_sign, ext_slt, disp, jump, branch};
  //   MemWrite = MemW; ALUscrB[1:0] = aluscr; 低六位[5:0] = \输入指令 [5:0]; 高6位[5:0] = \输入指令 [31:26]

  // Notes on the sheet:
  //   addi
  //   addiu
  //   andi
  //   ori
  //   lw
  //   sw
  //   beq
  //   bne
  //   slti
  //   j
  //   jl
  //   lh
  //   bgez
  //   add
  //   addu
  //   and
  //   sll
  //   sra
  //   srl
  //   sub
  //   or
  //   nor
  //   slt
  //   sltu
  //   jr
  //   srlv
  //   xor
  //   syscall
endmodule

module \寄存器堆  (
  input  [31:0] Din,
  input  clk,
  input  RegWrite,
  input  [4:0] R2,
  input  [4:0] W,
  input  [4:0] R1,
  output [31:0] RF_R1,
  output [31:0] RF_R2
);

  // RegisterFile registerfile_1: pin names not known; wires that end beside it: Din, clk, RegWrite, W, R1, R2, RF_R1, RF_R2
endmodule

// ALU
module alu (
  input  [31:0] X,
  input  [31:0] Y,
  input  [3:0] AluOP,
  output Signed_Overflow,
  output UnSigned_Overflow,
  output Equal,
  output [31:0] Result,
  output [31:0] Result_2
);

  wire and_2_out, and_3_out, comparator_1_lt, comparator_2_lt, comparator_3_lt, comparator_4_lt,
       comparator_5_gt, comparator_6_eq, comparator_7_eq, or_2_out, \和的溢出 , \差的溢出 ;
  wire [31:0] and_1_out, bit_extender_1_out, bit_extender_2_out, divider_1_out, multiplier_1_out, nor_1_out,
       or_1_out, shifter_1_out, shifter_2_out, shifter_3_out, xor_1_out, xor_2_out, \乘数高位 , \余数 , \和 , \差 ;

  // Probe on X
  // Probe on X
  // Probe on Y
  // Probe on Y
  Shifter #(.width(32)) shifter_1 (.in(X), .\dist (Y[4:0]), .out(shifter_1_out));
  Shifter #(.width(32), .shift("ar")) shifter_2 (.in(X), .\dist (Y[4:0]), .out(shifter_2_out));
  Shifter #(.width(32), .shift("lr")) shifter_3 (.in(X), .\dist (Y[4:0]), .out(shifter_3_out));
  Multiplier #(.width(32)) multiplier_1 (.a(X), .b(Y), .out(multiplier_1_out), .cout(\乘数高位 ));  // open: cin
  Divider #(.width(32)) divider_1 (.a(X), .b(Y), .out(divider_1_out), .rem(\余数 ));  // open: upper
  Adder #(.width(32)) adder_1 (.a(X), .b(Y), .out(\和 ), .cin(1'b0), .cout(\和的溢出 ));
  Adder #(.width(32)) adder_2 (.a(X), .b(xor_1_out), .out(\差 ), .cin(1'b1), .cout(\差的溢出 ));
  assign xor_1_out = Y ^ {32{1'b1}};  // XOR_Gate xor_1, 32 bits wide
  assign and_1_out = X & Y;  // AND_Gate and_1, 32 bits wide
  assign or_1_out = X | Y;  // OR_Gate or_1, 32 bits wide
  assign xor_2_out = X ^ Y;  // XOR_Gate xor_2, 32 bits wide
  assign nor_1_out = ~(X | Y);  // NOR_Gate nor_1, 32 bits wide
  Comparator #(.width(32)) comparator_1 (.a(X), .b(Y), .lt(comparator_1_lt));  // open: gt, eq
  Comparator #(.width(32), .mode("unsigned")) comparator_2 (
    .a(X), .b(Y), .eq(Equal), .lt(comparator_2_lt));  // open: gt
  assign bit_extender_1_out = {{31{1'b0}}, comparator_1_lt};  // Bit_Extender bit_extender_1
  assign bit_extender_2_out = {{31{1'b0}}, comparator_2_lt};  // Bit_Extender bit_extender_2
  // Probe on AluOP
  // Probe on Result
  // Probe on Result
  // Probe on Result_2
  Multiplexer #(.select(4), .width(32)) multiplexer_1 (
    .in0(shifter_1_out), .in1(shifter_2_out), .in2(shifter_3_out), .in3(multiplier_1_out),
    .in4(divider_1_out), .in5(\和 ), .in6(\差 ), .in7(and_1_out), .in8(or_1_out), .in9(xor_2_out),
    .in10(nor_1_out), .in11(bit_extender_1_out), .in12(bit_extender_2_out), .out(Result), .sel(AluOP));  // open: in13, in14, in15, en
  Comparator #(.width(32), .mode("unsigned")) comparator_3 (.a(\和 ), .b(X), .lt(comparator_3_lt));  // open: gt, eq
  Comparator #(.width(32), .mode("unsigned")) comparator_4 (.a(\和 ), .b(Y), .lt(comparator_4_lt));  // open: gt, eq
  Comparator #(.width(32), .mode("unsigned")) comparator_5 (.a(\差 ), .b(X), .gt(comparator_5_gt));  // open: eq, lt
  and and_2 (and_2_out, \和的溢出 , comparator_6_eq);
  Comparator #(.width(4)) comparator_6 (.a(AluOP), .b(4'b0101), .eq(comparator_6_eq));  // open: gt, lt
  and and_3 (and_3_out, \差的溢出 , comparator_7_eq);
  Comparator #(.width(4)) comparator_7 (.a(AluOP), .b(4'b0110), .eq(comparator_7_eq));  // open: gt, lt
  or or_2 (or_2_out, comparator_3_lt, comparator_4_lt);
  Multiplexer #(.select(4), .width(32)) multiplexer_2 (
    .in0({32{1'b0}}), .in1({32{1'b0}}), .in2({32{1'b0}}), .in3(\乘数高位 ), .in4(\余数 ), .in5({32{1'b0}}),
    .in6({32{1'b0}}), .in7({32{1'b0}}), .in8({32{1'b0}}), .in9({32{1'b0}}), .in10({32{1'b0}}),
    .in11({32{1'b0}}), .in12({32{1'b0}}), .in13({32{1'b0}}), .in14({32{1'b0}}), .in15({32{1'b0}}),
    .out(Result_2), .sel(AluOP));  // open: en
  Multiplexer #(.select(4)) multiplexer_3 (
    .in0(1'b0), .in1(1'b0), .in2(1'b0), .in3(1'b0), .in4(1'b0), .in5(or_2_out), .in6(comparator_5_gt),
    .in7(1'b0), .in8(1'b0), .in9(1'b0), .in10(1'b0), .in11(1'b0), .in12(1'b0), .in13(1'b0), .in14(1'b0),
    .in15(1'b0), .out(UnSigned_Overflow), .sel(AluOP));  // open: en
  or or_3 (Signed_Overflow, and_2_out, and_3_out);

  // Other names for the same wires on the sheet: OF = Signed_Overflow; Result2[31:0] = Result_2; S[3:0] = AluOP;
  //   UOF = UnSigned_Overflow

  // Notes on the sheet:
  //   不要改变此引脚区域内容，也不要改变ALU封装形式
  //   输入引脚
  //   乘数高32位
  //   余数
  //   请在下方利用上方输入输出引脚的隧道信号构建ALU电路，ctrl+d复制选择部件
  //   华中科技大学计算机学院 计算机组成原理，鸣谢加州大学伯克利CS61C课程
  //   逻辑左移
  //   算术右移
  //   逻辑右移
  //   乘数低32位
  //   商
  //   和
  //   差
  //   与
  //   或
  //   异或
  //   或非
  //   有符号比较 X<Y?1：0
  //   无符号比较X<Y?1:0
  //   输出引脚
  //   探测区域
endmodule

module IF_ID (
  input  [31:0] \指令 ,
  input  [31:0] PC_4,
  input  rst,
  input  clk,
  output [31:0] IR,
  output [31:0] PC_4_2
);

  wire [31:0] multiplexer_1_out;

  Multiplexer #(.width(32), .enable("false")) multiplexer_1 (
    .in0(\指令 ), .in1({32{1'b0}}), .out(multiplexer_1_out), .sel(rst));
  Multiplexer #(.width(32), .enable("false")) multiplexer_2 (.in0(PC_4), .in1({32{1'b0}}), .out(PC_4_2), .sel(rst));
  Register #(.width(32)) register_1 (.D(multiplexer_1_out), .Q(IR), .clk(clk));  // open: en, clr
  Register #(.width(32)) register_2 (.clk(clk));  // open: D, en, Q, clr
endmodule

module ID_EX (
  input  branch,
  input  [31:0] \无条件转移计算 ,
  input  junp,
  input  [31:0] PC_4,
  input  memW,
  input  [31:0] RF_R1,
  input  [3:0] aluop,
  input  [31:0] RF_R2,
  input  [1:0] rf_w,
  input  [31:0] ext,
  input  [1:0] aluscr,
  input  [9:0] rd_rt,
  input  systemcall,
  input  [1:0] regdst,
  input  regwrite,
  input  halt,
  input  rst,
  input  clk,
  output BRANCH_2,
  output [31:0] \无条件转移 ,
  output JUMP,
  output [31:0] PC_4_2,
  output MEMW_2,
  output [31:0] R1,
  output [3:0] ALUOP_2,
  output [31:0] R2,
  output [1:0] RF_W_2,
  output [31:0] ext_2,
  output [1:0] ALUSCR_2,
  output [9:0] RD_RT_2,
  output SYSCALL,
  output [1:0] REGDST_2,
  output REGWRITE_2,
  output halt_2
);

  wire multiplexer_8_out, multiplexer_9_out, multiplexer_10_out, multiplexer_11_out, multiplexer_15_out,
       multiplexer_16_out, not_1_out;
  wire [1:0] multiplexer_7_out, multiplexer_13_out, multiplexer_14_out;
  wire [3:0] multiplexer_12_out;
  wire [9:0] multiplexer_6_out;
  wire [31:0] multiplexer_3_out, multiplexer_4_out, multiplexer_5_out;

  Multiplexer #(.width(32), .enable("false")) multiplexer_1 (
    .in0(\无条件转移计算 ), .in1({32{1'b0}}), .out(\无条件转移 ), .sel(rst));
  Multiplexer #(.width(32), .enable("false")) multiplexer_2 (.in0(PC_4), .in1({32{1'b0}}), .out(PC_4_2), .sel(rst));
  Multiplexer #(.width(32), .enable("false")) multiplexer_3 (
    .in0(RF_R1), .in1({32{1'b0}}), .out(multiplexer_3_out), .sel(rst));
  Multiplexer #(.width(32), .enable("false")) multiplexer_4 (
    .in0(RF_R2), .in1({32{1'b0}}), .out(multiplexer_4_out), .sel(rst));
  Multiplexer #(.width(32), .enable("false")) multiplexer_5 (
    .in0(ext), .in1({32{1'b0}}), .out(multiplexer_5_out), .sel(rst));
  Multiplexer #(.width(10), .enable("false")) multiplexer_6 (
    .in0(rd_rt), .in1({10{1'b0}}), .out(multiplexer_6_out), .sel(rst));
  Multiplexer #(.width(2), .enable("false")) multiplexer_7 (
    .in0(regdst), .in1(2'b00), .out(multiplexer_7_out), .sel(rst));
  Multiplexer #(.enable("false")) multiplexer_8 (.in0(halt), .in1(1'b0), .out(multiplexer_8_out), .sel(rst));
  not not_1 (not_1_out, halt_2);
  Register #(.width(32)) register_1 (.en(not_1_out), .clk(clk));  // open: D, Q, clr
  Register #(.width(32)) register_2 (.en(not_1_out), .clk(clk));  // open: D, Q, clr
  Register #(.width(32)) register_3 (.D(multiplexer_3_out), .en(not_1_out), .Q(R1), .clk(clk));  // open: clr
  Register #(.width(32)) register_4 (.D(multiplexer_4_out), .en(not_1_out), .Q(R2), .clk(clk));  // open: clr
  Register #(.width(32)) register_5 (.D(multiplexer_5_out), .en(not_1_out), .Q(ext_2), .clk(clk));  // open: clr
  Register #(.width(10)) register_6 (.D(multiplexer_6_out), .en(not_1_out), .Q(RD_RT_2), .clk(clk));  // open: clr
  Register #(.width(2)) register_7 (.D(multiplexer_7_out), .en(not_1_out), .Q(REGDST_2), .clk(clk));  // open: clr
  Register #(.width(1)) register_8 (.D(multiplexer_8_out), .en(not_1_out), .Q(halt_2), .clk(clk));  // open: clr
  Multiplexer #(.enable("false")) multiplexer_9 (.in0(branch), .in1(1'b0), .out(multiplexer_9_out), .sel(rst));
  Multiplexer #(.enable("false")) multiplexer_10 (.in0(junp), .in1(1'b0), .out(multiplexer_10_out), .sel(rst));
  Multiplexer #(.enable("false")) multiplexer_11 (.in0(memW), .in1(1'b0), .out(multiplexer_11_out), .sel(rst));
  Multiplexer #(.width(4), .enable("false")) multiplexer_12 (
    .in0(aluop), .in1(4'b0000), .out(multiplexer_12_out), .sel(rst));
  Multiplexer #(.width(2), .enable("false")) multiplexer_13 (
    .in0(rf_w), .in1(2'b00), .out(multiplexer_13_out), .sel(rst));
  Multiplexer #(.width(2), .enable("false")) multiplexer_14 (
    .in0(aluscr), .in1(2'b00), .out(multiplexer_14_out), .sel(rst));
  Multiplexer #(.enable("false")) multiplexer_15 (.in0(systemcall), .in1(1'b0), .out(multiplexer_15_out), .sel(rst));
  Multiplexer #(.enable("false")) multiplexer_16 (.in0(regwrite), .in1(1'b0), .out(multiplexer_16_out), .sel(rst));
  Register #(.width(1)) register_9 (.D(multiplexer_9_out), .en(not_1_out), .Q(BRANCH_2), .clk(clk));  // open: clr
  Register #(.width(1)) register_10 (.D(multiplexer_10_out), .en(not_1_out), .Q(JUMP), .clk(clk));  // open: clr
  Register #(.width(1)) register_11 (.D(multiplexer_11_out), .en(not_1_out), .Q(MEMW_2), .clk(clk));  // open: clr
  Register #(.width(4)) register_12 (.D(multiplexer_12_out), .en(not_1_out), .Q(ALUOP_2), .clk(clk));  // open: clr
  Register #(.width(2)) register_13 (.D(multiplexer_13_out), .en(not_1_out), .Q(RF_W_2), .clk(clk));  // open: clr
  Register #(.width(2)) register_14 (.D(multiplexer_14_out), .en(not_1_out), .Q(ALUSCR_2), .clk(clk));  // open: clr
  Register #(.width(1)) register_15 (.D(multiplexer_15_out), .en(not_1_out), .Q(SYSCALL), .clk(clk));  // open: clr
  Register #(.width(1)) register_16 (.D(multiplexer_16_out), .en(not_1_out), .Q(REGWRITE_2), .clk(clk));  // open: clr
endmodule

// EX.MEM
module EX_MEM (
  input  [31:0] jump_to,
  input  [9:0] rd_rt,
  input  [31:0] PC_4,
  input  [1:0] regdst,
  input  [31:0] aluresult,
  input  regwrite,
  input  [23:0] alu24,
  input  memw,
  input  [1:0] rf_w,
  input  [31:0] r2,
  input  syscall,
  input  halt,
  input  rst,
  input  clk,
  output [31:0] JUMPTO,
  output [9:0] RD_RT_2,
  output [31:0] PC_4_2,
  output [1:0] REGDST_2,
  output [31:0] ALURESULT_2,
  output REGWRITE_2,
  output [23:0] ALU24_2,
  output MEMW_2,
  output [1:0] RF_W_2,
  output [31:0] R2_2,
  output SYSCALL_2,
  output halt_2
);

  wire multiplexer_6_out, multiplexer_9_out, multiplexer_10_out, multiplexer_11_out, not_1_out;
  wire [1:0] multiplexer_8_out, multiplexer_12_out;
  wire [9:0] multiplexer_7_out;
  wire [23:0] multiplexer_4_out;
  wire [31:0] multiplexer_2_out, multiplexer_3_out, multiplexer_5_out;

  Multiplexer #(.width(32), .enable("false")) multiplexer_1 (.in0(jump_to), .in1({32{1'b0}}), .out(JUMPTO), .sel(rst));
  Multiplexer #(.width(32), .enable("false")) multiplexer_2 (
    .in0(PC_4), .in1({32{1'b0}}), .out(multiplexer_2_out), .sel(rst));
  Multiplexer #(.width(32), .enable("false")) multiplexer_3 (
    .in0(aluresult), .in1({32{1'b0}}), .out(multiplexer_3_out), .sel(rst));
  Multiplexer #(.width(24), .enable("false")) multiplexer_4 (
    .in0(alu24), .in1({24{1'b0}}), .out(multiplexer_4_out), .sel(rst));
  Multiplexer #(.width(32), .enable("false")) multiplexer_5 (
    .in0(r2), .in1({32{1'b0}}), .out(multiplexer_5_out), .sel(rst));
  Multiplexer #(.enable("false")) multiplexer_6 (.in0(halt), .in1(1'b0), .out(multiplexer_6_out), .sel(rst));
  not not_1 (not_1_out, halt_2);
  Register #(.width(32)) register_1 (.en(not_1_out), .clk(clk));  // open: D, Q, clr
  Register #(.width(32)) register_2 (.D(multiplexer_2_out), .en(not_1_out), .Q(PC_4_2), .clk(clk));  // open: clr
  Register #(.width(32)) register_3 (.D(multiplexer_3_out), .en(not_1_out), .Q(ALURESULT_2), .clk(clk));  // open: clr
  Register #(.width(24)) register_4 (.D(multiplexer_4_out), .en(not_1_out), .Q(ALU24_2), .clk(clk));  // open: clr
  Register #(.width(32)) register_5 (.D(multiplexer_5_out), .en(not_1_out), .Q(R2_2), .clk(clk));  // open: clr
  Register #(.width(1)) register_6 (.D(multiplexer_6_out), .en(not_1_out), .Q(halt_2), .clk(clk));  // open: clr
  Multiplexer #(.width(10), .enable("false")) multiplexer_7 (
    .in0(rd_rt), .in1({10{1'b0}}), .out(multiplexer_7_out), .sel(rst));
  Multiplexer #(.width(2), .enable("false")) multiplexer_8 (
    .in0(regdst), .in1(2'b00), .out(multiplexer_8_out), .sel(rst));
  Multiplexer #(.enable("false")) multiplexer_9 (.in0(regwrite), .in1(1'b0), .out(multiplexer_9_out), .sel(rst));
  Multiplexer #(.enable("false")) multiplexer_10 (.in0(memw), .in1(1'b0), .out(multiplexer_10_out), .sel(rst));
  Multiplexer #(.enable("false")) multiplexer_11 (.in0(syscall), .in1(1'b0), .out(multiplexer_11_out), .sel(rst));
  Multiplexer #(.width(2), .enable("false")) multiplexer_12 (
    .in0(rf_w), .in1(2'b00), .out(multiplexer_12_out), .sel(rst));
  Register #(.width(10)) register_7 (.D(multiplexer_7_out), .en(not_1_out), .Q(RD_RT_2), .clk(clk));  // open: clr
  Register #(.width(2)) register_8 (.D(multiplexer_8_out), .en(not_1_out), .Q(REGDST_2), .clk(clk));  // open: clr
  Register #(.width(1)) register_9 (.D(multiplexer_9_out), .en(not_1_out), .Q(REGWRITE_2), .clk(clk));  // open: clr
  Register #(.width(1)) register_10 (.D(multiplexer_10_out), .en(not_1_out), .Q(MEMW_2), .clk(clk));  // open: clr
  Register #(.width(2)) register_11 (.D(multiplexer_12_out), .en(not_1_out), .Q(RF_W_2), .clk(clk));  // open: clr
  Register #(.width(1)) register_12 (.D(multiplexer_11_out), .en(not_1_out), .Q(SYSCALL_2), .clk(clk));  // open: clr
endmodule

module MEM_WB (
  input  [9:0] rd_rt,
  input  [31:0] PC_4,
  input  [1:0] regdst,
  input  [31:0] aluresult,
  input  regwrite,
  input  [1:0] rf_w,
  input  [31:0] data,
  input  sysycall,
  input  halt,
  input  rst,
  input  clk,
  output [9:0] RD_RT_2,
  output [31:0] PC_4_2,
  output [1:0] REGDST_2,
  output [31:0] ALURESULT_2,
  output REGWRITE_2,
  output [1:0] RF_W_2,
  output [31:0] DATA_2,
  output SYSCALL,
  output halt_2
);

  wire multiplexer_4_out, multiplexer_7_out, multiplexer_9_out, not_1_out;
  wire [1:0] multiplexer_6_out, multiplexer_8_out;
  wire [9:0] multiplexer_5_out;
  wire [31:0] multiplexer_1_out, multiplexer_2_out, multiplexer_3_out;

  Multiplexer #(.width(32), .enable("false")) multiplexer_1 (
    .in0(PC_4), .in1({32{1'b0}}), .out(multiplexer_1_out), .sel(rst));
  Multiplexer #(.width(32), .enable("false")) multiplexer_2 (
    .in0(aluresult), .in1({32{1'b0}}), .out(multiplexer_2_out), .sel(rst));
  Multiplexer #(.width(32), .enable("false")) multiplexer_3 (
    .in0(data), .in1({32{1'b0}}), .out(multiplexer_3_out), .sel(rst));
  Multiplexer #(.enable("false")) multiplexer_4 (.in0(halt), .in1(1'b0), .out(multiplexer_4_out), .sel(rst));
  not not_1 (not_1_out, halt_2);
  Register #(.width(32)) register_1 (.D(multiplexer_1_out), .en(not_1_out), .Q(PC_4_2), .clk(clk));  // open: clr
  Register #(.width(32)) register_2 (.D(multiplexer_2_out), .en(not_1_out), .Q(ALURESULT_2), .clk(clk));  // open: clr
  Register #(.width(32)) register_3 (.D(multiplexer_3_out), .en(not_1_out), .Q(DATA_2), .clk(clk));  // open: clr
  Register #(.width(1)) register_4 (.D(multiplexer_4_out), .en(not_1_out), .Q(halt_2), .clk(clk));  // open: clr
  Multiplexer #(.width(10), .enable("false")) multiplexer_5 (
    .in0(rd_rt), .in1({10{1'b0}}), .out(multiplexer_5_out), .sel(rst));
  Multiplexer #(.width(2), .enable("false")) multiplexer_6 (
    .in0(regdst), .in1(2'b00), .out(multiplexer_6_out), .sel(rst));
  Multiplexer #(.enable("false")) multiplexer_7 (.in0(regwrite), .in1(1'b0), .out(multiplexer_7_out), .sel(rst));
  Multiplexer #(.width(2), .enable("false")) multiplexer_8 (
    .in0(rf_w), .in1(2'b00), .out(multiplexer_8_out), .sel(rst));
  Multiplexer #(.enable("false")) multiplexer_9 (.in0(sysycall), .in1(1'b0), .out(multiplexer_9_out), .sel(rst));
  Register #(.width(10)) register_5 (.D(multiplexer_5_out), .en(not_1_out), .Q(RD_RT_2), .clk(clk));  // open: clr
  Register #(.width(2)) register_6 (.D(multiplexer_6_out), .en(not_1_out), .Q(REGDST_2), .clk(clk));  // open: clr
  Register #(.width(1)) register_7 (.D(multiplexer_7_out), .en(not_1_out), .Q(REGWRITE_2), .clk(clk));  // open: clr
  Register #(.width(2)) register_8 (.D(multiplexer_8_out), .en(not_1_out), .Q(RF_W_2), .clk(clk));  // open: clr
  Register #(.width(1)) register_9 (.D(multiplexer_9_out), .en(not_1_out), .Q(SYSCALL), .clk(clk));  // open: clr
endmodule
