// Logisim project 单周期CPU_ccmb.circ as structural Verilog: 8 circuits, main circuit main
module main (
);

  wire alu_1_equal, AluB_1, bat, branch, clk, DMWrite, go, jal, jump, nand_1_out, or_1_out, RegDin1, RegDst1,
       RegWrite, \return , RST, shift, syscall, \操作控制器_1_unsign ;
  wire [1:0] mode;
  wire [3:0] ALUOP;
  wire [4:0] multiplexer_3_out, multiplexer_4_out, multiplexer_5_out, registerfile_1_p6, \指令解析_1_out_3 ,
       \指令解析_1_out_4 , \指令解析_1_out_5 , \指令解析_1_out_6 ;
  wire [5:0] \指令解析_1_out_2 , \指令解析_1_out_7 ;
  wire [9:0] PC_q_2;
  wire [15:0] \总周期数 , \指令解析_1_out_8 , \无条件分支指令数 , \有条件分支成功跳转 , \有条件分支指令数 ;
  wire [25:0] \指令解析_1_out_9 ;
  wire [31:0] adder_1_out, alu_1_result, bit_extender_1_out, bit_extender_2_out, bit_extender_3_out,
       multiplexer_1_out, multiplexer_2_out, multiplexer_7_out, multiplexer_8_out, multiplexer_9_out,
       multiplexer_10_out, multiplexer_11_out, npc_1_pcout, PC_q, registerfile_1_p7, registerfile_1_p8,
       rom_1_data, SyscallOut, \数据存储器_1_dataout ;

  Button restart (.out(go));
  Register #(.width(32)) PC (
    .D(npc_1_pcout), .en(or_1_out), .Q({PC_q[31:12], PC_q_2, PC_q[1:0]}), .clk(clk), .clr(RST));
  Adder #(.width(32)) adder_1 (.a({PC_q[31:12], PC_q_2, PC_q[1:0]}), .b(32'h4), .out(adder_1_out));  // open: cin, cout
  \计数器  \u_计数器_1  (
    .clk(clk), .branch(branch), .jump(jump), .\总周期 (\总周期数 ), .RST(RST), .bat(bat), .\return (\return ),
    .\无条件 (\无条件分支指令数 ), .\有条件 (\有条件分支指令数 ), .halt(or_1_out), .\有条件成功 (\有条件分支成功跳转 ));
  Button \u_总复位  (.out(RST));
  Clock clock_1 (.out(clk));
  Hex_Digit_Display hex_digit_display_1 (.value(SyscallOut[31:28]));  // open: dp
  Hex_Digit_Display hex_digit_display_2 (.value(SyscallOut[27:24]));  // open: dp
  Multiplexer #(.width(32), .enable("false")) multiplexer_1 (
    .in0(alu_1_result), .in1(\数据存储器_1_dataout ), .out(multiplexer_1_out), .sel(RegDin1));
  Hex_Digit_Display hex_digit_display_3 (.value(SyscallOut[19:16]));  // open: dp
  Hex_Digit_Display hex_digit_display_4 (.value(SyscallOut[23:20]));  // open: dp
  Multiplexer #(.width(32), .enable("false")) multiplexer_2 (
    .in0(multiplexer_1_out), .in1(adder_1_out), .out(multiplexer_2_out), .sel(jal));
  Multiplexer #(.width(5), .enable("false")) multiplexer_3 (
    .in0(multiplexer_4_out), .in1({5{1'b1}}), .out(multiplexer_3_out), .sel(jal));
  Multiplexer #(.width(5), .enable("false")) multiplexer_4 (
    .in0(\指令解析_1_out_5 ), .in1(\指令解析_1_out_4 ), .out(multiplexer_4_out), .sel(RegDst1));
  ROM #(.addrWidth(10), .dataWidth(32)) rom_1 (.addr(PC_q_2), .data(rom_1_data));  // open: sel
  \指令解析  \u_指令解析_1  (
    .out_2(\指令解析_1_out_2 ), .\输入指令 (rom_1_data), .out_3(\指令解析_1_out_3 ), .out_4(\指令解析_1_out_4 ),
    .out_5(\指令解析_1_out_5 ), .out_6(\指令解析_1_out_6 ), .out_7(\指令解析_1_out_7 ), .out_8(\指令解析_1_out_8 ),
    .out_9(\指令解析_1_out_9 ));
  NPC npc_1 (
    .pc_4(adder_1_out), .imm26(\指令解析_1_out_9 ), ._16_32(multiplexer_7_out), .reg2(registerfile_1_p7),
    .pcout(npc_1_pcout), .jump(jump), .branch(branch), .\return (\return ));
  Hex_Digit_Display hex_digit_display_5 (.value(SyscallOut[11:8]));  // open: dp
  Hex_Digit_Display hex_digit_display_6 (.value(SyscallOut[15:12]));  // open: dp
  Multiplexer #(.width(5), .enable("false")) multiplexer_5 (
    .in0(\指令解析_1_out_3 ), .in1(5'b00010), .out(multiplexer_5_out), .sel(syscall));
  assign bit_extender_1_out = {{16{\指令解析_1_out_8 [15]}}, \指令解析_1_out_8 };  // Bit_Extender bit_extender_1
  assign bit_extender_2_out = {{16{1'b0}}, \指令解析_1_out_8 };  // Bit_Extender bit_extender_2
  assign bit_extender_3_out = {{27{1'b0}}, \指令解析_1_out_6 };  // Bit_Extender bit_extender_3
  Hex_Digit_Display hex_digit_display_7 (.value(SyscallOut[3:0]));  // open: dp
  Hex_Digit_Display hex_digit_display_8 (.value(SyscallOut[7:4]));  // open: dp
  // RegisterFile registerfile_1: pin names not known; wires that end beside it: multiplexer_2_out, clk, RegWrite, multiplexer_3_out, multiplexer_5_out, registerfile_1_p6, registerfile_1_p7, registerfile_1_p8
  Multiplexer #(.width(5), .enable("false")) multiplexer_6 (
    .in0(\指令解析_1_out_4 ), .in1(5'b00100), .out(registerfile_1_p6), .sel(syscall));
  Multiplexer #(.width(32), .enable("false")) multiplexer_7 (
    .in0(bit_extender_1_out), .in1(bit_extender_2_out), .out(multiplexer_7_out), .sel(\操作控制器_1_unsign ));
  Multiplexer #(.width(32), .enable("false")) multiplexer_8 (
    .in0(registerfile_1_p8), .in1(multiplexer_9_out), .out(multiplexer_8_out), .sel(AluB_1));
  Multiplexer #(.width(32), .enable("false")) multiplexer_9 (
    .in0(multiplexer_7_out), .in1(bit_extender_3_out), .out(multiplexer_9_out), .sel(shift));
  // Probe on \总周期数 
  // Probe on \无条件分支指令数 
  // Probe on \有条件分支指令数 
  // Probe on \有条件分支成功跳转 
  Multiplexer #(.width(32), .enable("false")) multiplexer_10 (
    .in0(registerfile_1_p7), .in1(registerfile_1_p8), .out(multiplexer_10_out), .sel(shift));
  ALU alu_1 (
    .AluOP(ALUOP), .X(multiplexer_10_out), .Equal(alu_1_equal), .Result(alu_1_result), .Y(multiplexer_11_out));  // open: Signed_Overflow, Result_2, UnSigned_Overflow
  Multiplexer #(.width(32), .enable("false")) multiplexer_11 (
    .in0(multiplexer_8_out), .in1(32'ha), .out(multiplexer_11_out), .sel(syscall));
  nand nand_1 (nand_1_out, syscall, alu_1_equal);
  or or_1 (or_1_out, go, nand_1_out);
  \操作控制器  \u_操作控制器_1  (
    .in_1(\指令解析_1_out_2 ), .jump(jump), .branch(branch), .\return (\return ), .RegDst1(RegDst1), .JAL(jal),
    .RegDin1(RegDin1), .in_4(\指令解析_1_out_7 ), .shift(shift), .ALUOP(ALUOP), .sys(syscall),
    .alur(alu_1_result), .in_3(alu_1_equal), .RegWrite(RegWrite), .DMWrite(DMWrite), .mode(mode),
    .bat_2(bat), .bat(AluB_1), .unsign(\操作控制器_1_unsign ));
  \数据存储器  \u_数据存储器_1  (
    .\字节地址 (alu_1_result[11:0]), .Din(registerfile_1_p8), .DataOut(\数据存储器_1_dataout ), .CLK(clk),
    .WE(DMWrite), .Mode(mode), .clr(RST));
  \显示器  \u_显示器_1  (
    .syscallout(SyscallOut), .sys(syscall), .clk(clk), .in_3(alu_1_equal), .rst(RST), .reg2(registerfile_1_p8));

  // Notes on the sheet:
  //   指令存储器IM
  //   contents of rom_1 (hex, n*v repeats v):
  //   20110001 8000c05 20110001 20120002 20130003 8000c09 20110001 20120002 20130003 8000c0d 20110001
  //   20120002 20130003 8000c11 20110001 20120002 20130003 c000cf3 20100001 20110001 118fc0 112020
  //   20020022 c 118882 12200001 8000c15 112020 20020022 c 20110001 118880 112020 20020022 c 12200001
  //   8000c1f 20110001 118fc0 112020 20020022 c 1188c3 112020 20020022 c 118903 112020 20020022 c 118903
  //   112020 20020022 c 118903 112020 20020022 c 118903 112020 20020022 c 118903 112020 20020022 c 118903
  //   112020 20020022 c 118903 112020 20020022 c 20100001 109fc0 139fc3 8021 2012000c 24160003 26100001
  //   3210000f 20080008 20090001 139900 2709825 132020 20020022 c 1094022 1500fff9 22100001 2018000f
  //   2188024 108700 20080008 20090001 139902 2709825 132021 20020022 c 1094022 1500fff9 108702 2c9b022
  //   12c00001 8000c50 4020 1084027 84400 3508ffff 82021 20020022 c 2010ffff 20110000 ae300000 22100001
  //   22310004 ae300000 22100001 22310004 ae300000 22100001 22310004 ae300000 22100001 22310004 ae300000
  //   22100001 22310004 ae300000 22100001 22310004 ae300000 22100001 22310004 ae300000 22100001 22310004
  //   ae300000 22100001 22310004 ae300000 22100001 22310004 ae300000 22100001 22310004 ae300000 22100001
  //   22310004 ae300000 22100001 22310004 ae300000 22100001 22310004 ae300000 22100001 22310004 ae300000
  //   22100001 22310004 22100001 8020 2011003c 8e130000 8e340000 274402a 11000002 ae330000 ae140000
  //   2231fffc 1611fff8 102020 20020022 c 22100004 2011003c 1611fff2 2002000a c 2011fff1 112020 20020022 c
  //   22310001 1a20fffb 2002000a c 20090000 200b0010 34118483 20120404 118c00 129400 36318281 22520404
  //   ad310000 2328820 21290004 216bffff 1560fffb 200b0020 20090000 91310000 112020 20020022 c 21290001
  //   216bffff 1560fff9 2002000a c 2008ffff 20090000 20111997 112020 20020022 c 2288820 2e291949 1120fffa
  //   2002000a c 2008ffff 20117777 112020 20020022 c 200b0010 3a31ffff 112020 20020022 c 216bffff 1560fffa
  //   2002000a c 2002000a c 20100000 22100001 102020 20020022 c 22100002 102020 20020022 c 22100003 102020
  //   20020022 c 22100004 102020 20020022 c 22100005 102020 20020022 c 22100006 102020 20020022 c 22100007
  //   102020 20020022 c 22100008 102020 20020022 20020022 c 3e00008
  //   数码管输出
  //   寄存器文件
endmodule

module \指令解析  (
  input  [31:0] \输入指令 ,
  output [5:0] out_2,
  output [4:0] out_3,
  output [4:0] out_4,
  output [4:0] out_5,
  output [4:0] out_6,
  output [5:0] out_7,
  output [15:0] out_8,
  output [25:0] out_9
);


  assign out_2 = \输入指令 [31:26];
  assign out_3 = \输入指令 [25:21];
  assign out_4 = \输入指令 [20:16];
  assign out_5 = \输入指令 [15:11];
  assign out_6 = \输入指令 [10:6];
  assign out_7 = \输入指令 [5:0];
  assign out_8 = \输入指令 [15:0];
  assign out_9 = \输入指令 [25:0];

  // Other names for the same wires on the sheet: func[5:0] = \输入指令 [5:0]; ins16[15:0] = \输入指令 [15:0];
  //   ins26[25:0] = \输入指令 [25:0]; 输入[31:0] = \输入指令 ; shamt[4:0] = \输入指令 [10:6]; rd[4:0] = \输入指令 [15:11];
  //   rt[4:0] = \输入指令 [20:16]; rs[4:0] = \输入指令 [25:21]; op[5:0] = \输入指令 [31:26]
endmodule

module \操作控制器  (
  input  [5:0] in_1,
  input  [31:0] alur,
  input  in_3,
  input  [5:0] in_4,
  output jump,
  output branch,
  output \return ,
  output RegDst1,
  output JAL,
  output RegDin1,
  output shift,
  output [3:0] ALUOP,
  output sys,
  output RegWrite,
  output DMWrite,
  output [1:0] mode,
  output bat,
  output bat_2,
  output unsign
);

  wire add, addi, addiu, addu, \and , and_14_out, and_15_out, and_16_out, and_17_out, andi, beq, blez, bne,
       buffer_1_out, comparator_17_eq, comparator_18_eq, comparator_19_eq, comparator_20_eq,
       comparator_21_eq, comparator_22_eq, comparator_23_eq, comparator_24_eq, comparator_25_eq,
       comparator_26_eq, comparator_27_eq, comparator_28_eq, comparator_29_eq, comparator_30_eq, j, lbu, lw,
       \nor , nor_1_out, not_1_out, not_2_out, \or , or_1_out, or_2_out, or_3_out, or_4_out, or_5_out,
       or_6_out, or_12_out, or_14_out, or_16_out, ori, r, sll, slt, slti, sltiu, sltu, sra, srl, sub, xori;

  Comparator #(.width(6)) comparator_1 (.a(in_1), .b({6{1'b0}}), .eq(r));  // open: gt, lt
  Comparator #(.width(6)) comparator_2 (.a(in_1), .b(6'b001000), .eq(addi));  // open: gt, lt
  Comparator #(.width(6)) comparator_3 (.a(in_1), .b(6'b001001), .eq(addiu));  // open: gt, lt
  Comparator #(.width(6)) comparator_4 (.a(in_1), .b(6'b001100), .eq(andi));  // open: gt, lt
  Comparator #(.width(6)) comparator_5 (.a(in_1), .b(6'b001101), .eq(ori));  // open: gt, lt
  Comparator #(.width(6)) comparator_6 (.a(in_1), .b(6'b001010), .eq(slti));  // open: gt, lt
  Comparator #(.width(6)) comparator_7 (.a(in_1), .b(6'b001110), .eq(xori));  // open: gt, lt
  Comparator #(.width(6)) comparator_8 (.a(in_1), .b(6'b001011), .eq(sltiu));  // open: gt, lt
  Comparator #(.width(6)) comparator_9 (.a(in_1), .b(6'b100011), .eq(lw));  // open: gt, lt
  Comparator #(.width(6)) comparator_10 (.a(in_1), .b(6'b101011), .eq(DMWrite));  // open: gt, lt
  Comparator #(.width(6)) comparator_11 (.a(in_1), .b(6'b100100), .eq(lbu));  // open: gt, lt
  Comparator #(.width(6)) comparator_12 (.a(in_1), .b(6'b000100), .eq(beq));  // open: gt, lt
  Comparator #(.width(6)) comparator_13 (.a(in_1), .b(6'b000101), .eq(bne));  // open: gt, lt
  Comparator #(.width(6)) comparator_14 (.a(in_1), .b(6'b000110), .eq(blez));  // open: gt, lt
  Comparator #(.width(6)) comparator_15 (.a(in_1), .b(6'b000010), .eq(j));  // open: gt, lt
  Comparator #(.width(6)) comparator_16 (.a(in_1), .b(6'b000011), .eq(JAL));  // open: gt, lt
  Comparator #(.width(6)) comparator_17 (.a(in_4), .b(6'b100000), .eq(comparator_17_eq));  // open: gt, lt
  Comparator #(.width(6)) comparator_18 (.a(in_4), .b(6'b100001), .eq(comparator_18_eq));  // open: gt, lt
  Comparator #(.width(6)) comparator_19 (.a(in_4), .b(6'b100100), .eq(comparator_19_eq));  // open: gt, lt
  Comparator #(.width(6)) comparator_20 (.a(in_4), .b({6{1'b0}}), .eq(comparator_20_eq));  // open: gt, lt
  Comparator #(.width(6)) comparator_21 (.a(in_4), .b(6'b000011), .eq(comparator_21_eq));  // open: gt, lt
  Comparator #(.width(6)) comparator_22 (.a(in_4), .b(6'b000010), .eq(comparator_22_eq));  // open: gt, lt
  Comparator #(.width(6)) comparator_23 (.a(in_4), .b(6'b100010), .eq(comparator_23_eq));  // open: gt, lt
  Comparator #(.width(6)) comparator_24 (.a(in_4), .b(6'b100101), .eq(comparator_24_eq));  // open: gt, lt
  Comparator #(.width(6)) comparator_25 (.a(in_4), .b(6'b100111), .eq(comparator_25_eq));  // open: gt, lt
  Comparator #(.width(6)) comparator_26 (.a(in_4), .b(6'b101010), .eq(comparator_26_eq));  // open: gt, lt
  Comparator #(.width(6)) comparator_27 (.a(in_4), .b(6'b101011), .eq(comparator_27_eq));  // open: gt, lt
  Comparator #(.width(6)) comparator_28 (.a(in_4), .b(6'b001000), .eq(comparator_28_eq));  // open: gt, lt
  Comparator #(.width(6)) comparator_29 (.a(in_4), .b(6'b001100), .eq(comparator_29_eq));  // open: gt, lt
  and and_1 (add, r, comparator_17_eq);
  and and_2 (addu, r, comparator_18_eq);
  and and_3 (\and , r, comparator_19_eq);
  and and_4 (sll, r, comparator_20_eq);
  and and_5 (sra, r, comparator_21_eq);
  and and_6 (srl, r, comparator_22_eq);
  and and_7 (sub, r, comparator_23_eq);
  and and_8 (\or , r, comparator_24_eq);
  and and_9 (\nor , r, comparator_25_eq);
  and and_10 (slt, r, comparator_26_eq);
  and and_11 (sltu, r, comparator_27_eq);
  and and_12 (\return , r, comparator_28_eq);
  and and_13 (sys, r, comparator_29_eq);
  assign ALUOP = sll ? 4'b0000 : 4'bz;  // Controlled_Buffer controlled_buffer_1
  assign ALUOP = sra ? 4'b0001 : 4'bz;  // Controlled_Buffer controlled_buffer_2
  assign ALUOP = srl ? 4'b0010 : 4'bz;  // Controlled_Buffer controlled_buffer_3
  assign ALUOP = or_1_out ? 4'b0101 : 4'bz;  // Controlled_Buffer controlled_buffer_4
  or or_1 (or_1_out, add, lw, addi, lbu, addiu, DMWrite, addu);
  assign ALUOP = sub ? 4'b0110 : 4'bz;  // Controlled_Buffer controlled_buffer_5
  assign ALUOP = or_2_out ? 4'b0111 : 4'bz;  // Controlled_Buffer controlled_buffer_6
  or or_2 (or_2_out, \and , andi);
  assign ALUOP = or_3_out ? 4'b1000 : 4'bz;  // Controlled_Buffer controlled_buffer_7
  or or_3 (or_3_out, \or , ori);
  assign ALUOP = xori ? 4'b1001 : 4'bz;  // Controlled_Buffer controlled_buffer_8
  assign ALUOP = \nor  ? 4'b1010 : 4'bz;  // Controlled_Buffer controlled_buffer_9
  assign ALUOP = or_4_out ? 4'b1011 : 4'bz;  // Controlled_Buffer controlled_buffer_10
  or or_4 (or_4_out, slt, blez, slti);
  assign ALUOP = or_5_out ? 4'b1100 : 4'bz;  // Controlled_Buffer controlled_buffer_11
  or or_5 (or_5_out, sltu, sltiu);
  assign ALUOP = or_6_out ? 4'b0000 : 4'bz;  // Controlled_Buffer controlled_buffer_12
  or or_6 (or_6_out, beq, j, bne, sys, \return , JAL);
  or or_7 (jump, j, JAL);
  or or_8 (RegDst1, addi, xori, addiu, sltiu, andi, lw, ori, lbu, slti);
  or or_9 (RegDin1, lw, lbu);
  or or_10 (bat, sll, addi, sltiu, addiu, lw, andi, sra, ori, DMWrite, slti, lbu, xori, srl);
  or or_11 (shift, sll, srl, sra);
  not not_1 (not_1_out, or_12_out);
  or or_12 (or_12_out, \return , sys);
  and and_14 (and_14_out, not_1_out, r);
  or or_13 (RegWrite, and_14_out, addi, xori, addiu, sltiu, JAL, andi, lw, ori, lbu, slti);
  Comparator #(.width(32)) comparator_30 (.a(32'h1), .b(alur), .eq(comparator_30_eq));  // open: gt, lt
  buf buffer_1 (buffer_1_out, lbu);
  or or_14 (or_14_out, DMWrite, lw);
  nor nor_1 (nor_1_out, lbu, lw, DMWrite);
  or or_15 (bat_2, beq, blez, bne);
  not not_2 (not_2_out, in_3);
  or or_16 (or_16_out, in_3, comparator_30_eq);
  assign mode = buffer_1_out ? 2'b01 : 2'bz;  // Controlled_Buffer controlled_buffer_13
  assign mode = or_14_out ? 2'b00 : 2'bz;  // Controlled_Buffer controlled_buffer_14
  assign mode = nor_1_out ? 2'b10 : 2'bz;  // Controlled_Buffer controlled_buffer_15
  and and_15 (and_15_out, beq, in_3);
  and and_16 (and_16_out, bne, not_2_out);
  and and_17 (and_17_out, blez, or_16_out);
  or or_17 (unsign, xori, lbu, andi, ori);
  or or_18 (branch, and_15_out, and_16_out, and_17_out);

  // Other names for the same wires on the sheet: AluB_1 = bat; bat_t = bat_2; func[5:0] = in_4; jr = \return ;
  //   op[5:0] = in_1; sw = DMWrite; syscall = sys; tunnel = in_3
endmodule

module \数据存储器  (
  input  [11:0] \字节地址 ,
  input  [31:0] Din,
  input  CLK,
  input  WE,
  input  [1:0] Mode,
  input  clr,
  output [31:0] DataOut
);

  wire and_1_out, and_2_out, and_3_out, and_4_out, and_5_out, and_6_out, and_7_out, and_8_out, and_9_out,
       and_10_out, and_11_out, and_12_out, and_13_out, and_14_out, buffer_1_out, buffer_2_out, buffer_7_out,
       buffer_8_out, buffer_9_out, buffer_10_out, buffer_11_out, CS0, CS1, CS2, CS3, decoder_1_out3,
       not_2_out, not_3_out, nWE, xor_1_out, \半字访问 , \字节访问 , \字访问 ;
  wire [7:0] buffer_3_out, D0, D1, D2, D3, DIN0, DIN1, DIN2, DIN3;
  wire [15:0] buffer_12_out;
  wire [31:0] bit_extender_1_out, bit_extender_2_out, buffer_14_out, demultiplexer_1_out0,
       demultiplexer_1_out1, demultiplexer_1_out2, demultiplexer_1_out3;

  not not_1 (nWE, WE);
  and and_1 (and_1_out, WE, CS3);
  and and_2 (and_2_out, WE, CS2);
  and and_3 (and_3_out, WE, CS1);
  and and_4 (and_4_out, WE, CS0);
  RAM #(.addrWidth(10), .bus("separate")) ram_1 (
    .addr(\字节地址 [11:2]), .din(DIN3), .data(D3), .str(and_1_out), .clk(CLK), .ld(and_5_out), .clr(clr));  // open: sel
  and and_5 (and_5_out, CS3, nWE);
  RAM #(.addrWidth(10), .bus("separate")) ram_2 (
    .addr(\字节地址 [11:2]), .din(DIN2), .data(D2), .str(and_2_out), .clk(CLK), .ld(and_6_out), .clr(clr));  // open: sel
  and and_6 (and_6_out, CS2, nWE);
  RAM #(.addrWidth(10), .bus("separate")) ram_3 (
    .addr(\字节地址 [11:2]), .din(DIN1), .data(D1), .str(and_3_out), .clk(CLK), .ld(and_7_out), .clr(clr));  // open: sel
  and and_7 (and_7_out, CS1, nWE);
  RAM #(.addrWidth(10), .bus("separate")) ram_4 (
    .addr(\字节地址 [11:2]), .din(DIN0), .data(D0), .str(and_4_out), .clk(CLK), .ld(and_8_out), .clr(clr));  // open: sel
  and and_8 (and_8_out, CS0, nWE);
  buf buffer_1 (buffer_1_out, \字访问 );
  buf buffer_2 (buffer_2_out, \字节访问 );
  assign buffer_3_out = D0;  // Buffer buffer_3, 8 bits wide
  assign buffer_3_out = D1;  // Buffer buffer_4, 8 bits wide
  assign buffer_3_out = D2;  // Buffer buffer_5, 8 bits wide
  assign buffer_3_out = D3;  // Buffer buffer_6, 8 bits wide
  Demultiplexer #(.select(2), .width(32), .enable("false")) demultiplexer_1 (
    .out0(demultiplexer_1_out0), .out1(demultiplexer_1_out1), .out2(demultiplexer_1_out2),
    .out3(demultiplexer_1_out3), .in(Din), .sel(Mode));
  // Probe on DataOut
  buf buffer_7 (buffer_7_out, buffer_1_out);
  and and_9 (and_9_out, \字节地址 [1], \半字访问 );
  buf buffer_8 (buffer_8_out, and_9_out);
  buf buffer_9 (buffer_9_out, \半字访问 );
  xor xor_1 (xor_1_out, \半字访问 , \字节地址 [1]);
  not not_2 (not_2_out, \字节地址 [0]);
  buf buffer_10 (buffer_10_out, \字节地址 [0]);
  buf buffer_11 (buffer_11_out, \字节地址 [1]);
  not not_3 (not_3_out, \字节地址 [1]);
  assign buffer_12_out = {D1, D0};  // Buffer buffer_12, 16 bits wide
  assign buffer_12_out = {D3, D2};  // Buffer buffer_13, 16 bits wide
  and and_10 (and_10_out, buffer_9_out, xor_1_out);
  assign buffer_14_out = {D3, D2, D1, D0};  // Buffer buffer_14, 32 bits wide
  assign bit_extender_1_out = {{24{1'b0}}, buffer_3_out};  // Bit_Extender bit_extender_1
  Multiplexer #(.select(2), .width(32), .enable("false")) multiplexer_1 (
    .in0(buffer_14_out), .in1(bit_extender_1_out), .in2(bit_extender_2_out), .in3({32{1'b0}}), .out(DataOut),
    .sel(Mode));
  assign bit_extender_2_out = {{16{1'b0}}, buffer_12_out};  // Bit_Extender bit_extender_2
  assign DIN0 = demultiplexer_1_out0[7:0] | demultiplexer_1_out1[7:0] | demultiplexer_1_out2[7:0];  // OR_Gate or_1, 8 bits wide
  assign DIN1 = demultiplexer_1_out0[15:8] | demultiplexer_1_out1[7:0] | demultiplexer_1_out2[15:8];  // OR_Gate or_2, 8 bits wide
  assign DIN2 = demultiplexer_1_out0[23:16] | demultiplexer_1_out1[7:0] | demultiplexer_1_out2[7:0];  // OR_Gate or_3, 8 bits wide
  assign DIN3 = demultiplexer_1_out0[31:24] | demultiplexer_1_out1[7:0] | demultiplexer_1_out2[15:8];  // OR_Gate or_4, 8 bits wide
  Decoder #(.select(2), .enable("false")) decoder_1 (
    .out0(\字访问 ), .out1(\字节访问 ), .out2(\半字访问 ), .out3(decoder_1_out3), .sel(Mode));
  and and_11 (and_11_out, buffer_2_out, buffer_10_out, buffer_11_out);
  and and_12 (and_12_out, buffer_2_out, not_2_out, buffer_11_out);
  and and_13 (and_13_out, buffer_2_out, buffer_10_out, not_3_out);
  and and_14 (and_14_out, not_2_out, not_3_out, buffer_2_out);
  or or_5 (CS3, buffer_7_out, buffer_8_out, and_11_out);
  or or_6 (CS2, buffer_7_out, buffer_8_out, and_12_out);
  or or_7 (CS1, buffer_7_out, and_10_out, and_13_out);
  or or_8 (CS0, buffer_7_out, and_10_out, and_14_out);

  // Other names for the same wires on the sheet: Dout[31:0] = DataOut; 字节选择[1:0] = \字节地址 [1:0]; 半字选择 = \字节地址 [1];
  //   字地址[9:0] = \字节地址 [11:2]

  // Notes on the sheet:
  //   输入引脚区
  //   请勿增改引脚，请勿修改子电路封装
  //   电路功能：利用下图中给定的RAM器件实现既既可以按照字节，也可以按照半字，也可以按照32位字访问的MIPS存储器
  //   请在下方利用上方输入输出引脚的隧道信号构建电路，ctrl+d复制选择部件
  //   输出引脚区
endmodule

module NPC (
  input  [31:0] pc_4,
  input  [25:0] imm26,
  input  [31:0] _16_32,
  input  [31:0] reg2,
  input  jump,
  input  branch,
  input  \return ,
  output [31:0] pcout
);

  wire [31:0] adder_1_out, multiplexer_2_out, multiplexer_3_out, shifter_1_out;

  Shifter #(.width(32)) shifter_1 (.in(_16_32), .\dist (5'b00010), .out(shifter_1_out));
  Multiplexer #(.width(32), .enable("false")) multiplexer_1 (
    .in0(multiplexer_2_out), .in1(reg2), .out(pcout), .sel(\return ));
  Adder #(.width(32)) adder_1 (.a(pc_4), .b(shifter_1_out), .out(adder_1_out));  // open: cin, cout
  Multiplexer #(.width(32), .enable("false")) multiplexer_2 (
    .in0(multiplexer_3_out), .in1({pc_4[31:28], imm26, 2'b00}), .out(multiplexer_2_out), .sel(jump));
  Multiplexer #(.width(32), .enable("false")) multiplexer_3 (
    .in0(pc_4), .in1(adder_1_out), .out(multiplexer_3_out), .sel(branch));
endmodule

module branch (
  input  beq,
  input  equ,
  input  bne,
  input  blez,
  input  c,
  output branch
);

  wire and_1_out, and_2_out, and_3_out, and_4_out, and_5_out, and_6_out, beq_t, blez_t, bne_t, branch_t,
       buffer_1_out, buffer_2_out, buffer_3_out, buffer_4_out, comparator_1_eq, not_1_out, not_2_out,
       or_1_out, or_3_out, tunnel;
  wire [31:0] alur;

  not not_1 (not_1_out, equ);
  or or_1 (or_1_out, equ, c);
  and and_1 (and_1_out, beq, equ);
  and and_2 (and_2_out, bne, not_1_out);
  and and_3 (and_3_out, blez, or_1_out);
  or or_2 (branch, and_1_out, and_2_out, and_3_out);
  buf buffer_1 (buffer_1_out, beq_t);
  and and_4 (and_4_out, buffer_1_out, buffer_2_out);
  buf buffer_2 (buffer_2_out, tunnel);
  not not_2 (not_2_out, tunnel);
  and and_5 (and_5_out, not_2_out, buffer_3_out);
  buf buffer_3 (buffer_3_out, bne_t);
  buf buffer_4 (buffer_4_out, blez_t);
  and and_6 (and_6_out, buffer_4_out, or_3_out);
  or or_3 (or_3_out, tunnel, comparator_1_eq);
  Comparator #(.width(32)) comparator_1 (.a(32'h1), .b(alur), .eq(comparator_1_eq));  // open: gt, lt
  or or_4 (branch_t, and_4_out, and_5_out, and_6_out);
endmodule

module \计数器  (
  input  clk,
  input  branch,
  input  jump,
  input  RST,
  input  bat,
  input  \return ,
  input  halt,
  output [15:0] \总周期 ,
  output [15:0] \无条件 ,
  output [15:0] \有条件 ,
  output [15:0] \有条件成功 
);

  wire or_1_out, or_2_out, register_1_q;

  Counter #(.width(16), .max('hffff)) counter_1 (
    .count(or_1_out), .Q(\无条件 ), .clk(clk), .clr(RST));  // open: load, D, carry
  or or_1 (or_1_out, jump, \return );
  Register #(.width(1)) register_1 (.D(halt), .Q(register_1_q), .clk(clk));  // open: en, clr
  Counter #(.width(16), .max('hffff)) counter_2 (
    .count(or_2_out), .Q(\总周期 ), .clk(clk), .clr(RST));  // open: load, D, carry
  or or_2 (or_2_out, halt, register_1_q);
  Counter #(.width(16), .max('hffff)) counter_3 (.count(bat), .Q(\有条件 ), .clk(clk), .clr(RST));  // open: load, D, carry
  Counter #(.width(16), .max('hffff)) counter_4 (
    .count(branch), .Q(\有条件成功 ), .clk(clk), .clr(RST));  // open: load, D, carry

  // Other names for the same wires on the sheet: 总周期数[15:0] = \总周期 ; 无条件分支指令数[15:0] = \无条件 ;
  //   有条件分支成功跳转[15:0] = \有条件成功 ; 有条件分支指令数[15:0] = \有条件 
endmodule

module \显示器  (
  input  sys,
  input  clk,
  input  in_3,
  input  rst,
  input  [31:0] reg2,
  output [31:0] syscallout
);

  wire and_1_out, not_1_out;

  not not_1 (not_1_out, in_3);
  Register #(.width(32)) register_1 (.D(reg2), .en(and_1_out), .Q(syscallout), .clk(clk), .clr(rst));
  and and_1 (and_1_out, sys, not_1_out);

  // Other names for the same wires on the sheet: syscall = sys; tunnel = in_3
endmodule
