// Logisim project 单级中断（bug）.circ as structural Verilog: 8 circuits, main circuit main
module main (
);

  wire alu_1_equal, AluB_1, and_1_out, and_2_out, and_3_out, and_4_out, and_5_out, bat, branch, clk,
       d_ff_1_q, d_ff_2_q, d_ff_3_q, d_ff_4_q, decoder_1_out1, decoder_1_out2, decoder_1_out3, DMWrite, eret,
       go, IE_q, IR, IR1, ir1_t, IR2, ir2_t, IR3, ir3_t, IR_CPU, jal, jump, nand_1_out, not_1_out, not_2_out,
       not_3_out, not_4_out, not_5_out, or_4_out, or_5_out, or_6_out, or_7_out, RegDin1, RegDst1, RegWrite,
       \return , RST, rst1, rst2, rst3, shift, syscall, w1, w2, w3, \操作控制器_1_unsign ;
  wire [1:0] curr_xy, mode, priority_encoder_1_out;
  wire [3:0] ALUOP;
  wire [4:0] multiplexer_6_out, multiplexer_7_out, multiplexer_8_out, registerfile_1_p6, \指令解析_1_out_3 ,
       \指令解析_1_out_4 , \指令解析_1_out_5 , \指令解析_1_out_6 ;
  wire [5:0] \指令解析_1_out_2 , \指令解析_1_out_7 ;
  wire [15:0] \总周期数 , \指令解析_1_out_8 , \无条件分支指令数 , \有条件分支成功跳转 , \有条件分支指令数 ;
  wire [25:0] \指令解析_1_out_9 ;
  wire [31:0] adder_2_out, alu_1_result, bit_extender_1_out, bit_extender_2_out, bit_extender_3_out, epc,
       multiplexer_2_out, multiplexer_3_out, multiplexer_4_out, multiplexer_5_out, multiplexer_10_out,
       multiplexer_11_out, multiplexer_12_out, multiplexer_13_out, multiplexer_14_out, npc_1_pcout, pc,
       realpc, registerfile_1_p7, registerfile_1_p8, rom_1_data, SyscallOut, \数据存储器_1_dataout ;

  Button _1 (.out(ir1_t));
  Button _2 (.out(ir2_t));
  Button _3 (.out(ir3_t));
  LED led_1 (.in(w1));
  LED led_2 (.in(w2));
  LED led_3 (.in(w3));
  Button \u_总复位  (.out(RST));
  Clock clock_1 (.out(clk));
  Button restart (.out(go));
  D_Flip_Flop d_ff_1 (.clk(ir1_t), .D(1'b1), .Q(d_ff_1_q), .reset(IR1));  // open: Qn, preset, en
  or or_1 (w1, IR1, d_ff_1_q);
  D_Flip_Flop d_ff_2 (.clk(ir2_t), .D(1'b1), .Q(d_ff_2_q), .reset(IR2));  // open: Qn, preset, en
  or or_2 (w2, IR2, d_ff_2_q);
  D_Flip_Flop d_ff_3 (.clk(ir3_t), .D(1'b1), .Q(d_ff_3_q), .reset(IR3));  // open: Qn, preset, en
  or or_3 (w3, IR3, d_ff_3_q);
  Hex_Digit_Display hex_digit_display_1 (.value(SyscallOut[31:28]));  // open: dp
  // Probe on curr_xy
  not not_1 (not_1_out, eret);
  Hex_Digit_Display hex_digit_display_2 (.value(SyscallOut[23:20]));  // open: dp
  Hex_Digit_Display hex_digit_display_3 (.value(SyscallOut[27:24]));  // open: dp
  D_Flip_Flop d_ff_4 (.clk(clk), .D(and_1_out), .Q(d_ff_4_q), .en(IR_CPU));  // open: Qn, preset, reset
  Register #(.width(32)) u_EPC (.D(pc), .en(and_1_out), .Q(epc), .clk(clk));  // open: clr
  and and_1 (and_1_out, not_1_out, IR_CPU);
  or or_4 (or_4_out, d_ff_1_q, IR1);
  or or_5 (or_5_out, d_ff_2_q, IR2);
  or or_6 (or_6_out, d_ff_3_q, IR3);
  Hex_Digit_Display hex_digit_display_4 (.value(SyscallOut[15:12]));  // open: dp
  Hex_Digit_Display hex_digit_display_5 (.value(SyscallOut[19:16]));  // open: dp
  Priority_Encoder #(.select(2)) priority_encoder_1 (
    .in0(1'b0), .in1(IR1), .in2(IR2), .in3(IR3), .out(priority_encoder_1_out), .gs(IR));  // open: en_out, en_in
  D_Flip_Flop IE (.clk(clk), .D(1'b1), .Q(IE_q), .preset(eret), .en(not_2_out), .reset(and_2_out));  // open: Qn
  not not_2 (not_2_out, IE_q);
  and and_2 (and_2_out, not_1_out, d_ff_4_q);
  and and_3 (and_3_out, or_4_out, not_3_out);
  not not_3 (not_3_out, rst1);
  and and_4 (and_4_out, or_5_out, not_4_out);
  not not_4 (not_4_out, rst2);
  and and_5 (and_5_out, or_6_out, not_5_out);
  not not_5 (not_5_out, rst3);
  Hex_Digit_Display hex_digit_display_6 (.value(SyscallOut[11:8]));  // open: dp
  Hex_Digit_Display hex_digit_display_7 (.value(SyscallOut[7:4]));  // open: dp
  and and_6 (IR_CPU, IR, IE_q);
  D_Flip_Flop u_IR1 (.clk(clk), .D(and_3_out), .Q(IR1));  // open: Qn, preset, en, reset
  D_Flip_Flop u_IR2 (.clk(clk), .D(and_4_out), .Q(IR2));  // open: Qn, preset, en, reset
  D_Flip_Flop u_IR3 (.clk(clk), .D(and_5_out), .Q(IR3));  // open: Qn, preset, en, reset
  Hex_Digit_Display hex_digit_display_8 (.value(SyscallOut[3:0]));  // open: dp
  Decoder #(.select(2), .enable("false")) decoder_1 (
    .out1(decoder_1_out1), .out2(decoder_1_out2), .out3(decoder_1_out3), .sel(curr_xy));  // open: out0
  Register #(.width(2)) EPC_2 (.D(priority_encoder_1_out), .Q(curr_xy), .clk(and_1_out));  // open: en, clr
  // Probe on \总周期数 
  // Probe on \无条件分支指令数 
  // Probe on \有条件分支指令数 
  // Probe on \有条件分支成功跳转 
  and and_7 (rst1, eret, decoder_1_out1);
  and and_8 (rst2, decoder_1_out2, eret);
  and and_9 (rst3, decoder_1_out3, eret);
  Multiplexer #(.select(2), .width(32), .enable("false")) multiplexer_1 (
    .in1(32'h4), .in2(32'h1c8), .in3(32'h38c), .out(realpc), .sel(priority_encoder_1_out));  // open: in0
  Multiplexer #(.width(32), .enable("false")) multiplexer_2 (
    .in0(npc_1_pcout), .in1(realpc), .out(multiplexer_2_out), .sel(IR_CPU));
  Adder #(.width(32)) adder_1 (.a(32'h4), .b(npc_1_pcout));  // open: out, cin, cout
  Register #(.width(32)) u_PC (.D(multiplexer_3_out), .en(or_7_out), .Q(pc), .clk(clk), .clr(RST));
  Multiplexer #(.width(32), .enable("false")) multiplexer_3 (
    .in0(multiplexer_2_out), .in1(epc), .out(multiplexer_3_out), .sel(eret));
  Adder #(.width(32)) adder_2 (.a(32'h4), .b(pc), .out(adder_2_out));  // open: cin, cout
  Multiplexer #(.width(32), .enable("false")) multiplexer_4 (
    .in0(alu_1_result), .in1(\数据存储器_1_dataout ), .out(multiplexer_4_out), .sel(RegDin1));
  \计数器  \u_计数器_1  (
    .clk(clk), .branch(branch), .jump(jump), .\总周期 (\总周期数 ), .RST(RST), .bat(bat), .\return (\return ),
    .\无条件 (\无条件分支指令数 ), .\有条件 (\有条件分支指令数 ), .halt(or_7_out), .\有条件成功 (\有条件分支成功跳转 ));
  Multiplexer #(.width(32), .enable("false")) multiplexer_5 (
    .in0(multiplexer_4_out), .in1(adder_2_out), .out(multiplexer_5_out), .sel(jal));
  Multiplexer #(.width(5), .enable("false")) multiplexer_6 (
    .in0(multiplexer_7_out), .in1({5{1'b1}}), .out(multiplexer_6_out), .sel(jal));
  Multiplexer #(.width(5), .enable("false")) multiplexer_7 (
    .in0(\指令解析_1_out_5 ), .in1(\指令解析_1_out_4 ), .out(multiplexer_7_out), .sel(RegDst1));
  ROM #(.addrWidth(10), .dataWidth(32)) rom_1 (.addr(pc[11:2]), .data(rom_1_data));  // open: sel
  \指令解析  \u_指令解析_1  (
    .out_2(\指令解析_1_out_2 ), .\输入指令 (rom_1_data), .out_3(\指令解析_1_out_3 ), .out_4(\指令解析_1_out_4 ),
    .out_5(\指令解析_1_out_5 ), .out_6(\指令解析_1_out_6 ), .out_7(\指令解析_1_out_7 ), .out_8(\指令解析_1_out_8 ),
    .out_9(\指令解析_1_out_9 ));
  NPC npc_1 (
    .pc_4(adder_2_out), .imm26(\指令解析_1_out_9 ), ._16_32(multiplexer_10_out), .reg2(registerfile_1_p7),
    .pcout(npc_1_pcout), .jump(jump), .branch(branch), .\return (\return ));
  Multiplexer #(.width(5), .enable("false")) multiplexer_8 (
    .in0(\指令解析_1_out_3 ), .in1(5'b00010), .out(multiplexer_8_out), .sel(syscall));
  assign bit_extender_1_out = {{16{\指令解析_1_out_8 [15]}}, \指令解析_1_out_8 };  // Bit_Extender bit_extender_1
  assign bit_extender_2_out = {{16{1'b0}}, \指令解析_1_out_8 };  // Bit_Extender bit_extender_2
  assign bit_extender_3_out = {{27{1'b0}}, \指令解析_1_out_6 };  // Bit_Extender bit_extender_3
  // RegisterFile registerfile_1: pin names not known; wires that end beside it: multiplexer_5_out, clk, RegWrite, multiplexer_6_out, multiplexer_8_out, registerfile_1_p6, registerfile_1_p7, registerfile_1_p8
  Multiplexer #(.width(5), .enable("false")) multiplexer_9 (
    .in0(\指令解析_1_out_4 ), .in1(5'b00100), .out(registerfile_1_p6), .sel(syscall));
  Multiplexer #(.width(32), .enable("false")) multiplexer_10 (
    .in0(bit_extender_1_out), .in1(bit_extender_2_out), .out(multiplexer_10_out), .sel(\操作控制器_1_unsign ));
  Multiplexer #(.width(32), .enable("false")) multiplexer_11 (
    .in0(registerfile_1_p8), .in1(multiplexer_12_out), .out(multiplexer_11_out), .sel(AluB_1));
  Multiplexer #(.width(32), .enable("false")) multiplexer_12 (
    .in0(multiplexer_10_out), .in1(bit_extender_3_out), .out(multiplexer_12_out), .sel(shift));
  Multiplexer #(.width(32), .enable("false")) multiplexer_13 (
    .in0(registerfile_1_p7), .in1(registerfile_1_p8), .out(multiplexer_13_out), .sel(shift));
  Multiplexer #(.width(32), .enable("false")) multiplexer_14 (
    .in0(multiplexer_11_out), .in1(32'ha), .out(multiplexer_14_out), .sel(syscall));
  nand nand_1 (nand_1_out, syscall, alu_1_equal);
  or or_7 (or_7_out, go, nand_1_out);
  ALU alu_1 (
    .AluOP(ALUOP), .X(multiplexer_13_out), .Equal(alu_1_equal), .Result(alu_1_result), .Y(multiplexer_14_out));  // open: Signed_Overflow, Result_2, UnSigned_Overflow
  \操作控制器  \u_操作控制器_1  (
    .op(\指令解析_1_out_2 ), .jump(jump), .branch(branch), .\return (\return ), .RegDst1(RegDst1), .JAL(jal),
    .RegDin1(RegDin1), .func(\指令解析_1_out_7 ), .shift(shift), .ALUOP(ALUOP), .sys(syscall),
    .alur(alu_1_result), .in_4(alu_1_equal), .RegWrite(RegWrite), .DMWrite(DMWrite), .mode(mode),
    .bat_2(bat), .bat(AluB_1), .unsign(\操作控制器_1_unsign ), .rs(\指令解析_1_out_3 ), .eret(eret));
  \数据存储器  \u_数据存储器_1  (
    .\字节地址 (alu_1_result[11:0]), .Din(registerfile_1_p8), .DataOut(\数据存储器_1_dataout ), .CLK(clk),
    .WE(DMWrite), .Mode(mode), .clr(RST));
  \显示器  \u_显示器_1  (
    .syscallout(SyscallOut), .sys(syscall), .clk(clk), .in_3(alu_1_equal), .rst(RST), .reg2(registerfile_1_p8));

  // Notes on the sheet:
  //   指令存储器IM
  //   contents of rom_1 (hex, n*v repeats v):
  //   8000d54 23bdfffc afa10000 23bdfffc afa20000 23bdfffc afa30000 23bdfffc afa40000 23bdfffc afa50000
  //   23bdfffc afa60000 23bdfffc afa70000 23bdfffc afa80000 23bdfffc afa90000 23bdfffc afaa0000 23bdfffc
  //   afab0000 23bdfffc afac0000 23bdfffc afad0000 23bdfffc afae0000 23bdfffc afaf0000 23bdfffc afb00000
  //   23bdfffc afb10000 23bdfffc afb20000 23bdfffc afb30000 23bdfffc afb40000 23bdfffc afb50000 23bdfffc
  //   afb60000 23bdfffc afb70000 23bdfffc afb80000 23bdfffc afb90000 20160001 20140006 20150001 168020
  //   108100 2149825 132020 20020022 c 1600fffa 295a022 1680fff7 8fb90000 23bd0004 8fb80000 23bd0004
  //   8fb70000 23bd0004 8fb60000 23bd0004 8fb50000 23bd0004 8fb40000 23bd0004 8fb30000 23bd0004 8fb20000
  //   23bd0004 8fb10000 23bd0004 8fb00000 23bd0004 8faf0000 23bd0004 8fae0000 23bd0004 8fad0000 23bd0004
  //   8fac0000 23bd0004 8fab0000 23bd0004 8faa0000 23bd0004 8fa90000 23bd0004 8fa80000 23bd0004 8fa70000
  //   23bd0004 8fa60000 23bd0004 8fa50000 23bd0004 8fa40000 23bd0004 8fa30000 23bd0004 8fa20000 23bd0004
  //   8fa10000 23bd0004 42000018 23bdfffc afa10000 23bdfffc afa20000 23bdfffc afa30000 23bdfffc afa40000
  //   23bdfffc afa50000 23bdfffc afa60000 23bdfffc afa70000 23bdfffc afa80000 23bdfffc afa90000 23bdfffc
  //   afaa0000 23bdfffc afab0000 23bdfffc afac0000 23bdfffc afad0000 23bdfffc afae0000 23bdfffc afaf0000
  //   23bdfffc afb00000 23bdfffc afb10000 23bdfffc afb20000 23bdfffc afb30000 23bdfffc afb40000 23bdfffc
  //   afb50000 23bdfffc afb60000 23bdfffc afb70000 23bdfffc afb80000 23bdfffc afb90000 20160002 20140006
  //   20150001 168020 108100 2149825 132020 20020022 c 1600fffa 295a022 1680fff7 8fb90000 23bd0004
  //   8fb80000 23bd0004 8fb70000 23bd0004 8fb60000 23bd0004 8fb50000 23bd0004 8fb40000 23bd0004 8fb30000
  //   23bd0004 8fb20000 23bd0004 8fb10000 23bd0004 8fb00000 23bd0004 8faf0000 23bd0004 8fae0000 23bd0004
  //   8fad0000 23bd0004 8fac0000 23bd0004 8fab0000 23bd0004 8faa0000 23bd0004 8fa90000 23bd0004 8fa80000
  //   23bd0004 8fa70000 23bd0004 8fa60000 23bd0004 8fa50000 23bd0004 8fa40000 23bd0004 8fa30000 23bd0004
  //   8fa20000 23bd0004 8fa10000 23bd0004 42000018 23bdfffc afa10000 23bdfffc afa20000 23bdfffc afa30000
  //   23bdfffc afa40000 23bdfffc afa50000 23bdfffc afa60000 23bdfffc afa70000 23bdfffc afa80000 23bdfffc
  //   afa90000 23bdfffc afaa0000 23bdfffc afab0000 23bdfffc afac0000 23bdfffc afad0000 23bdfffc afae0000
  //   23bdfffc afaf0000 23bdfffc afb00000 23bdfffc afb10000 23bdfffc afb20000 23bdfffc afb30000 23bdfffc
  //   afb40000 23bdfffc afb50000 23bdfffc afb60000 23bdfffc afb70000 23bdfffc afb80000 23bdfffc afb90000
  //   20160003 20140006 20150001 168020 108100 2149825 132020 20020022 c 1600fffa 295a022 1680fff7
  //   8fb90000 23bd0004 8fb80000 23bd0004 8fb70000 23bd0004 8fb60000 23bd0004 8fb50000 23bd0004 8fb40000
  //   23bd0004 8fb30000 23bd0004 8fb20000 23bd0004 8fb10000 23bd0004 8fb00000 23bd0004 8faf0000 23bd0004
  //   8fae0000 23bd0004 8fad0000 23bd0004 8fac0000 23bd0004 8fab0000 23bd0004 8faa0000 23bd0004 8fa90000
  //   23bd0004 8fa80000 23bd0004 8fa70000 23bd0004 8fa60000 23bd0004 8fa50000 23bd0004 8fa40000 23bd0004
  //   8fa30000 23bd0004 8fa20000 23bd0004 8fa10000 23bd0004 42000018 20110200 20020022 112020 c 2231ffff
  //   1620fffc 20020032 c 2002000a c
  //   寄存器文件
endmodule

module \指令解析  (
  input  [31:0] \输入指令 ,
  output [5:0] out_2,
  output [4:0] out_3,
  output [4:0] out_4,
  output [4:0] out_5,
  output [4:0] out_6,
  output [5:0] out_7,
  output [15:0] out_8,
  output [25:0] out_9
);


  assign out_2 = \输入指令 [31:26];
  assign out_3 = \输入指令 [25:21];
  assign out_4 = \输入指令 [20:16];
  assign out_5 = \输入指令 [15:11];
  assign out_6 = \输入指令 [10:6];
  assign out_7 = \输入指令 [5:0];
  assign out_8 = \输入指令 [15:0];
  assign out_9 = \输入指令 [25:0];

  // Other names for the same wires on the sheet: func[5:0] = \输入指令 [5:0]; ins16[15:0] = \输入指令 [15:0];
  //   ins26[25:0] = \输入指令 [25:0]; 输入[31:0] = \输入指令 ; shamt[4:0] = \输入指令 [10:6]; rd[4:0] = \输入指令 [15:11];
  //   rt[4:0] = \输入指令 [20:16]; rs[4:0] = \输入指令 [25:21]; op[5:0] = \输入指令 [31:26]
endmodule

module \操作控制器  (
  input  [5:0] op,
  input  [5:0] func,
  input  [31:0] alur,
  input  in_4,
  input  [4:0] rs,
  output jump,
  output branch,
  output \return ,
  output RegDst1,
  output JAL,
  output RegDin1,
  output shift,
  output [3:0] ALUOP,
  output sys,
  output RegWrite,
  output DMWrite,
  output [1:0] mode,
  output bat,
  output bat_2,
  output eret,
  output unsign
);

  wire add, addi, addiu, addu, \and , and_17_out, and_18_out, and_19_out, and_20_out, andi, beq, blez, bne,
       buffer_1_out, comparator_18_eq, comparator_19_eq, comparator_20_eq, comparator_21_eq,
       comparator_22_eq, comparator_23_eq, comparator_24_eq, comparator_25_eq, comparator_26_eq,
       comparator_27_eq, comparator_28_eq, comparator_29_eq, comparator_30_eq, comparator_31_eq,
       comparator_32_eq, comparator_33_eq, comparator_34_eq, ir, j, lbu, lw, mfc0, mtc0, \nor , nor_1_out,
       not_1_out, not_2_out, \or , or_6_out, or_8_out, or_10_out, or_13_out, or_14_out, or_15_out, or_16_out,
       or_17_out, or_18_out, ori, r, sll, slt, slti, sltiu, sltu, sra, srl, sub, xori;

  Comparator #(.width(6)) comparator_1 (.a(op), .b({6{1'b0}}), .eq(r));  // open: gt, lt
  Comparator #(.width(6)) comparator_2 (.a(op), .b(6'b001000), .eq(addi));  // open: gt, lt
  Comparator #(.width(6)) comparator_3 (.a(op), .b(6'b001001), .eq(addiu));  // open: gt, lt
  Comparator #(.width(6)) comparator_4 (.a(op), .b(6'b001100), .eq(andi));  // open: gt, lt
  Comparator #(.width(6)) comparator_5 (.a(op), .b(6'b001101), .eq(ori));  // open: gt, lt
  Comparator #(.width(6)) comparator_6 (.a(op), .b(6'b001010), .eq(slti));  // open: gt, lt
  Comparator #(.width(6)) comparator_7 (.a(op), .b(6'b001110), .eq(xori));  // open: gt, lt
  Comparator #(.width(6)) comparator_8 (.a(op), .b(6'b001011), .eq(sltiu));  // open: gt, lt
  Comparator #(.width(6)) comparator_9 (.a(op), .b(6'b010000), .eq(ir));  // open: gt, lt
  Comparator #(.width(6)) comparator_10 (.a(op), .b(6'b100011), .eq(lw));  // open: gt, lt
  Comparator #(.width(6)) comparator_11 (.a(op), .b(6'b101011), .eq(DMWrite));  // open: gt, lt
  Comparator #(.width(6)) comparator_12 (.a(op), .b(6'b100100), .eq(lbu));  // open: gt, lt
  Comparator #(.width(6)) comparator_13 (.a(op), .b(6'b000100), .eq(beq));  // open: gt, lt
  Comparator #(.width(6)) comparator_14 (.a(op), .b(6'b000101), .eq(bne));  // open: gt, lt
  Comparator #(.width(6)) comparator_15 (.a(op), .b(6'b000110), .eq(blez));  // open: gt, lt
  Comparator #(.width(6)) comparator_16 (.a(op), .b(6'b000010), .eq(j));  // open: gt, lt
  Comparator #(.width(6)) comparator_17 (.a(op), .b(6'b000011), .eq(JAL));  // open: gt, lt
  Comparator #(.width(6)) comparator_18 (.a(func), .b(6'b100000), .eq(comparator_18_eq));  // open: gt, lt
  Comparator #(.width(6)) comparator_19 (.a(func), .b(6'b100001), .eq(comparator_19_eq));  // open: gt, lt
  Comparator #(.width(6)) comparator_20 (.a(func), .b(6'b100100), .eq(comparator_20_eq));  // open: gt, lt
  Comparator #(.width(6)) comparator_21 (.a(func), .b({6{1'b0}}), .eq(comparator_21_eq));  // open: gt, lt
  Comparator #(.width(6)) comparator_22 (.a(func), .b(6'b000011), .eq(comparator_22_eq));  // open: gt, lt
  Comparator #(.width(6)) comparator_23 (.a(func), .b(6'b000010), .eq(comparator_23_eq));  // open: gt, lt
  Comparator #(.width(6)) comparator_24 (.a(func), .b(6'b100010), .eq(comparator_24_eq));  // open: gt, lt
  Comparator #(.width(6)) comparator_25 (.a(func), .b(6'b100101), .eq(comparator_25_eq));  // open: gt, lt
  Comparator #(.width(6)) comparator_26 (.a(func), .b(6'b100111), .eq(comparator_26_eq));  // open: gt, lt
  Comparator #(.width(6)) comparator_27 (.a(func), .b(6'b101010), .eq(comparator_27_eq));  // open: gt, lt
  Comparator #(.width(6)) comparator_28 (.a(func), .b(6'b101011), .eq(comparator_28_eq));  // open: gt, lt
  Comparator #(.width(6)) comparator_29 (.a(func), .b(6'b001000), .eq(comparator_29_eq));  // open: gt, lt
  Comparator #(.width(6)) comparator_30 (.a(func), .b(6'b001100), .eq(comparator_30_eq));  // open: gt, lt
  Comparator #(.width(5)) comparator_31 (.a(rs), .b({5{1'b0}}), .eq(comparator_31_eq));  // open: gt, lt
  Comparator #(.width(5)) comparator_32 (.a(rs), .b(5'b00100), .eq(comparator_32_eq));  // open: gt, lt
  Comparator #(.width(5)) comparator_33 (.a(rs), .b(5'b10000), .eq(comparator_33_eq));  // open: gt, lt
  and and_1 (add, r, comparator_18_eq);
  and and_2 (addu, r, comparator_19_eq);
  and and_3 (\and , r, comparator_20_eq);
  and and_4 (sll, r, comparator_21_eq);
  and and_5 (sra, r, comparator_22_eq);
  and and_6 (srl, r, comparator_23_eq);
  and and_7 (sub, r, comparator_24_eq);
  and and_8 (\or , r, comparator_25_eq);
  and and_9 (\nor , r, comparator_26_eq);
  and and_10 (slt, r, comparator_27_eq);
  and and_11 (sltu, r, comparator_28_eq);
  and and_12 (\return , r, comparator_29_eq);
  and and_13 (sys, r, comparator_30_eq);
  and and_14 (mfc0, ir, comparator_31_eq);
  and and_15 (mtc0, ir, comparator_32_eq);
  and and_16 (eret, ir, comparator_33_eq);
  or or_1 (jump, j, JAL);
  or or_2 (RegDst1, addi, xori, addiu, sltiu, andi, lw, ori, lbu, slti);
  or or_3 (RegDin1, lw, lbu);
  or or_4 (bat, sll, addi, sltiu, addiu, lw, andi, sra, ori, DMWrite, slti, lbu, xori, srl);
  or or_5 (shift, sll, srl, sra);
  not not_1 (not_1_out, or_6_out);
  or or_6 (or_6_out, \return , sys);
  and and_17 (and_17_out, not_1_out, r);
  or or_7 (RegWrite, and_17_out, addi, xori, addiu, sltiu, JAL, andi, lw, ori, lbu, slti);
  Comparator #(.width(32)) comparator_34 (.a(32'h1), .b(alur), .eq(comparator_34_eq));  // open: gt, lt
  buf buffer_1 (buffer_1_out, lbu);
  or or_8 (or_8_out, DMWrite, lw);
  nor nor_1 (nor_1_out, lbu, lw, DMWrite);
  or or_9 (bat_2, beq, blez, bne);
  not not_2 (not_2_out, in_4);
  or or_10 (or_10_out, in_4, comparator_34_eq);
  assign mode = buffer_1_out ? 2'b01 : 2'bz;  // Controlled_Buffer controlled_buffer_1
  assign mode = or_8_out ? 2'b00 : 2'bz;  // Controlled_Buffer controlled_buffer_2
  assign mode = nor_1_out ? 2'b10 : 2'bz;  // Controlled_Buffer controlled_buffer_3
  and and_18 (and_18_out, beq, in_4);
  and and_19 (and_19_out, bne, not_2_out);
  and and_20 (and_20_out, blez, or_10_out);
  or or_11 (unsign, xori, lbu, andi, ori);
  or or_12 (branch, and_18_out, and_19_out, and_20_out);
  assign ALUOP = sll ? 4'b0000 : 4'bz;  // Controlled_Buffer controlled_buffer_4
  assign ALUOP = sra ? 4'b0001 : 4'bz;  // Controlled_Buffer controlled_buffer_5
  assign ALUOP = srl ? 4'b0010 : 4'bz;  // Controlled_Buffer controlled_buffer_6
  assign ALUOP = or_13_out ? 4'b0101 : 4'bz;  // Controlled_Buffer controlled_buffer_7
  or or_13 (or_13_out, add, lw, addi, lbu, addiu, DMWrite, addu);
  assign ALUOP = sub ? 4'b0110 : 4'bz;  // Controlled_Buffer controlled_buffer_8
  assign ALUOP = or_14_out ? 4'b0111 : 4'bz;  // Controlled_Buffer controlled_buffer_9
  or or_14 (or_14_out, \and , andi);
  assign ALUOP = or_15_out ? 4'b1000 : 4'bz;  // Controlled_Buffer controlled_buffer_10
  or or_15 (or_15_out, \or , ori);
  assign ALUOP = xori ? 4'b1001 : 4'bz;  // Controlled_Buffer controlled_buffer_11
  assign ALUOP = \nor  ? 4'b1010 : 4'bz;  // Controlled_Buffer controlled_buffer_12
  assign ALUOP = or_16_out ? 4'b1011 : 4'bz;  // Controlled_Buffer controlled_buffer_13
  or or_16 (or_16_out, slt, blez, slti);
  assign ALUOP = or_17_out ? 4'b1100 : 4'bz;  // Controlled_Buffer controlled_buffer_14
  or or_17 (or_17_out, sltu, sltiu);
  assign ALUOP = or_18_out ? 4'b0000 : 4'bz;  // Controlled_Buffer controlled_buffer_15
  or or_18 (or_18_out, beq, j, bne, sys, \return , JAL);

  // Other names for the same wires on the sheet: AluB_1 = bat; bat_t = bat_2; jr = \return ; sw = DMWrite;
  //   syscall = sys; tunnel = in_4
endmodule

module \数据存储器  (
  input  [11:0] \字节地址 ,
  input  [31:0] Din,
  input  CLK,
  input  WE,
  input  [1:0] Mode,
  input  clr,
  output [31:0] DataOut
);

  wire and_1_out, and_2_out, and_3_out, and_4_out, and_5_out, and_6_out, and_7_out, and_8_out, and_9_out,
       and_10_out, and_11_out, and_12_out, and_13_out, and_14_out, buffer_1_out, buffer_2_out, buffer_7_out,
       buffer_8_out, buffer_9_out, buffer_10_out, buffer_11_out, CS0, CS1, CS2, CS3, decoder_1_out3,
       not_2_out, not_3_out, nWE, xor_1_out, \半字访问 , \字节访问 , \字访问 ;
  wire [7:0] buffer_3_out, D0, D1, D2, D3, DIN0, DIN1, DIN2, DIN3;
  wire [15:0] buffer_12_out;
  wire [31:0] bit_extender_1_out, bit_extender_2_out, buffer_14_out, demultiplexer_1_out0,
       demultiplexer_1_out1, demultiplexer_1_out2, demultiplexer_1_out3;

  not not_1 (nWE, WE);
  and and_1 (and_1_out, WE, CS3);
  and and_2 (and_2_out, WE, CS2);
  and and_3 (and_3_out, WE, CS1);
  and and_4 (and_4_out, WE, CS0);
  RAM #(.addrWidth(10), .bus("separate")) ram_1 (
    .addr(\字节地址 [11:2]), .din(DIN3), .data(D3), .str(and_1_out), .clk(CLK), .ld(and_5_out), .clr(clr));  // open: sel
  and and_5 (and_5_out, CS3, nWE);
  RAM #(.addrWidth(10), .bus("separate")) ram_2 (
    .addr(\字节地址 [11:2]), .din(DIN2), .data(D2), .str(and_2_out), .clk(CLK), .ld(and_6_out), .clr(clr));  // open: sel
  and and_6 (and_6_out, CS2, nWE);
  RAM #(.addrWidth(10), .bus("separate")) ram_3 (
    .addr(\字节地址 [11:2]), .din(DIN1), .data(D1), .str(and_3_out), .clk(CLK), .ld(and_7_out), .clr(clr));  // open: sel
  and and_7 (and_7_out, CS1, nWE);
  RAM #(.addrWidth(10), .bus("separate")) ram_4 (
    .addr(\字节地址 [11:2]), .din(DIN0), .data(D0), .str(and_4_out), .clk(CLK), .ld(and_8_out), .clr(clr));  // open: sel
  and and_8 (and_8_out, CS0, nWE);
  buf buffer_1 (buffer_1_out, \字访问 );
  buf buffer_2 (buffer_2_out, \字节访问 );
  assign buffer_3_out = D0;  // Buffer buffer_3, 8 bits wide
  assign buffer_3_out = D1;  // Buffer buffer_4, 8 bits wide
  assign buffer_3_out = D2;  // Buffer buffer_5, 8 bits wide
  assign buffer_3_out = D3;  // Buffer buffer_6, 8 bits wide
  Demultiplexer #(.select(2), .width(32), .enable("false")) demultiplexer_1 (
    .out0(demultiplexer_1_out0), .out1(demultiplexer_1_out1), .out2(demultiplexer_1_out2),
    .out3(demultiplexer_1_out3), .in(Din), .sel(Mode));
  // Probe on DataOut
  buf buffer_7 (buffer_7_out, buffer_1_out);
  and and_9 (and_9_out, \字节地址 [1], \半字访问 );
  buf buffer_8 (buffer_8_out, and_9_out);
  buf buffer_9 (buffer_9_out, \半字访问 );
  xor xor_1 (xor_1_out, \半字访问 , \字节地址 [1]);
  not not_2 (not_2_out, \字节地址 [0]);
  buf buffer_10 (buffer_10_out, \字节地址 [0]);
  buf buffer_11 (buffer_11_out, \字节地址 [1]);
  not not_3 (not_3_out, \字节地址 [1]);
  assign buffer_12_out = {D1, D0};  // Buffer buffer_12, 16 bits wide
  assign buffer_12_out = {D3, D2};  // Buffer buffer_13, 16 bits wide
  and and_10 (and_10_out, buffer_9_out, xor_1_out);
  assign buffer_14_out = {D3, D2, D1, D0};  // Buffer buffer_14, 32 bits wide
  assign bit_extender_1_out = {{24{1'b0}}, buffer_3_out};  // Bit_Extender bit_extender_1
  Multiplexer #(.select(2), .width(32), .enable("false")) multiplexer_1 (
    .in0(buffer_14_out), .in1(bit_extender_1_out), .in2(bit_extender_2_out), .in3({32{1'b0}}), .out(DataOut),
    .sel(Mode));
  assign bit_extender_2_out = {{16{1'b0}}, buffer_12_out};  // Bit_Extender bit_extender_2
  assign DIN0 = demultiplexer_1_out0[7:0] | demultiplexer_1_out1[7:0] | demultiplexer_1_out2[7:0];  // OR_Gate or_1, 8 bits wide
  assign DIN1 = demultiplexer_1_out0[15:8] | demultiplexer_1_out1[7:0] | demultiplexer_1_out2[15:8];  // OR_Gate or_2, 8 bits wide
  assign DIN2 = demultiplexer_1_out0[23:16] | demultiplexer_1_out1[7:0] | demultiplexer_1_out2[7:0];  // OR_Gate or_3, 8 bits wide
  assign DIN3 = demultiplexer_1_out0[31:24] | demultiplexer_1_out1[7:0] | demultiplexer_1_out2[15:8];  // OR_Gate or_4, 8 bits wide
  Decoder #(.select(2), .enable("false")) decoder_1 (
    .out0(\字访问 ), .out1(\字节访问 ), .out2(\半字访问 ), .out3(decoder_1_out3), .sel(Mode));
  and and_11 (and_11_out, buffer_2_out, buffer_10_out, buffer_11_out);
  and and_12 (and_12_out, buffer_2_out, not_2_out, buffer_11_out);
  and and_13 (and_13_out, buffer_2_out, buffer_10_out, not_3_out);
  and and_14 (and_14_out, not_2_out, not_3_out, buffer_2_out);
  or or_5 (CS3, buffer_7_out, buffer_8_out, and_11_out);
  or or_6 (CS2, buffer_7_out, buffer_8_out, and_12_out);
  or or_7 (CS1, buffer_7_out, and_10_out, and_13_out);
  or or_8 (CS0, buffer_7_out, and_10_out, and_14_out);

  // Other names for the same wires on the sheet: Dout[31:0] = DataOut; 字节选择[1:0] = \字节地址 [1:0]; 半字选择 = \字节地址 [1];
  //   字地址[9:0] = \字节地址 [11:2]

  // Notes on the sheet:
  //   输入引脚区
  //   请勿增改引脚，请勿修改子电路封装
  //   电路功能：利用下图中给定的RAM器件实现既既可以按照字节，也可以按照半字，也可以按照32位字访问的MIPS存储器
  //   请在下方利用上方输入输出引脚的隧道信号构建电路，ctrl+d复制选择部件
  //   输出引脚区
endmodule

module NPC (
  input  [31:0] pc_4,
  input  [25:0] imm26,
  input  [31:0] _16_32,
  input  [31:0] reg2,
  input  jump,
  input  branch,
  input  \return ,
  output [31:0] pcout
);

  wire [31:0] adder_1_out, multiplexer_2_out, multiplexer_3_out, shifter_1_out;

  Shifter #(.width(32)) shifter_1 (.in(_16_32), .\dist (5'b00010), .out(shifter_1_out));
  Multiplexer #(.width(32), .enable("false")) multiplexer_1 (
    .in0(multiplexer_2_out), .in1(reg2), .out(pcout), .sel(\return ));
  Adder #(.width(32)) adder_1 (.a(pc_4), .b(shifter_1_out), .out(adder_1_out));  // open: cin, cout
  Multiplexer #(.width(32), .enable("false")) multiplexer_2 (
    .in0(multiplexer_3_out), .in1({pc_4[31:28], imm26, 2'b00}), .out(multiplexer_2_out), .sel(jump));
  Multiplexer #(.width(32), .enable("false")) multiplexer_3 (
    .in0(pc_4), .in1(adder_1_out), .out(multiplexer_3_out), .sel(branch));
endmodule

module \计数器  (
  input  clk,
  input  branch,
  input  jump,
  input  RST,
  input  bat,
  input  \return ,
  input  halt,
  output [15:0] \总周期 ,
  output [15:0] \无条件 ,
  output [15:0] \有条件 ,
  output [15:0] \有条件成功 
);

  wire or_1_out, or_2_out, register_1_q;

  Counter #(.width(16), .max('hffff)) counter_1 (
    .count(or_1_out), .Q(\无条件 ), .clk(clk), .clr(RST));  // open: load, D, carry
  or or_1 (or_1_out, jump, \return );
  Register #(.width(1)) register_1 (.D(halt), .Q(register_1_q), .clk(clk));  // open: en, clr
  Counter #(.width(16), .max('hffff)) counter_2 (
    .count(or_2_out), .Q(\总周期 ), .clk(clk), .clr(RST));  // open: load, D, carry
  or or_2 (or_2_out, halt, register_1_q);
  Counter #(.width(16), .max('hffff)) counter_3 (.count(bat), .Q(\有条件 ), .clk(clk), .clr(RST));  // open: load, D, carry
  Counter #(.width(16), .max('hffff)) counter_4 (
    .count(branch), .Q(\有条件成功 ), .clk(clk), .clr(RST));  // open: load, D, carry

  // Other names for the same wires on the sheet: 总周期数[15:0] = \总周期 ; 无条件分支指令数[15:0] = \无条件 ;
  //   有条件分支成功跳转[15:0] = \有条件成功 ; 有条件分支指令数[15:0] = \有条件 
endmodule

module \显示器  (
  input  sys,
  input  clk,
  input  in_3,
  input  rst,
  input  [31:0] reg2,
  output [31:0] syscallout
);

  wire and_1_out, not_1_out;

  not not_1 (not_1_out, in_3);
  Register #(.width(32)) register_1 (.D(reg2), .en(and_1_out), .Q(syscallout), .clk(clk), .clr(rst));
  and and_1 (and_1_out, sys, not_1_out);

  // Other names for the same wires on the sheet: syscall = sys; tunnel = in_3
endmodule

module tmp (
);

  wire and_1_out, eret, IE_q, not_1_out, not_2_out, undriven, undriven_2;
  wire [31:0] epc, pc;

  // OR_Gate or_1 has open pins: in0=eret, in1=not_2_out, out=open
  not not_1 (not_1_out, eret);
  D_Flip_Flop IE (.clk(undriven), .D(1'b1), .Q(IE_q), .en(undriven_2));  // open: Qn, preset, reset
  Register #(.width(32)) u_EPC (.D(pc), .en(undriven_2), .Q(epc), .clk(undriven));  // open: clr
  not not_2 (not_2_out, undriven_2);
  and and_1 (and_1_out, not_1_out, IE_q);
endmodule
